// Logisim project Cache.circ as structural Verilog: 6 circuits, main circuit Cache
module Cache (
  input  [31:0] Addr,
  input  [31:0] Data_in,
  input  clk,
  input  HitBit,
  input  MemWrite,
  input  MemRead,
  output out_7,
  output [31:0] out_8,
  output [15:0] out_9,
  output [15:0] out_10
);

  wire and_1_out, and_2_out, decoder_1_out0, decoder_1_out1, decoder_1_out2, decoder_1_out3, en1, en2, en3,
       en4, Hit, Hit1, Hit2, Hit3, Hit4, or_1_out;
  wire [1:0] or_3_out;
  wire [31:0] group_1_out_12, group_1_out_13, group_1_out_14, group_1_out_15, group_2_out_12, group_2_out_13,
       group_2_out_14, group_2_out_15, group_3_out_12, group_3_out_13, group_3_out_14, group_3_out_15,
       group_4_out_12, group_4_out_13, group_4_out_14, group_4_out_15, multiplexer_1_out, multiplexer_2_out,
       multiplexer_3_out, multiplexer_4_out, multiplexer_5_out, multiplexer_6_out, ram_1__1, ram_1__2,
       ram_1__3, ram_1__4;

  and and_1 (and_1_out, MemRead, ~out_7);  // AND_Gate
  and and_2 (and_2_out, MemRead, Hit, ~out_7);  // AND_Gate
  Decoder #(.select(2)) decoder_1 (
    .out0(decoder_1_out0), .out1(decoder_1_out1), .out2(decoder_1_out2), .out3(decoder_1_out3),
    .sel(Addr[5:4]));  // open: en
  or or_1 (or_1_out, MemWrite, MemRead);
  Counter_part #(.width(16), .max('hffff)) counter_1 (
    .count(and_1_out), .Q(out_9), .clk(clk), .clr(HitBit));  // open: load, D, carry
  Counter_part #(.width(16), .max('hffff)) counter_2 (
    .count(and_2_out), .Q(out_10), .clk(clk), .clr(HitBit));  // open: load, D, carry
  and and_3 (en1, decoder_1_out0, or_1_out);
  and and_4 (en4, decoder_1_out3, or_1_out);
  RAM ram_1 (
    .MuxBlock(Addr[3:2]), .MemWrite(MemWrite), .MemRead(MemRead), .Hit(Hit), .Tag(Addr[11:6]),
    .MuxGroup(Addr[5:4]), .MemData(Data_in), .Clk(clk), .Reset(HitBit), ._4(ram_1__4), ._3(ram_1__3),
    ._2(ram_1__2), .out_13(out_7), ._1(ram_1__1));
  and and_5 (en2, decoder_1_out1, or_1_out);
  and and_6 (en3, decoder_1_out2, or_1_out);
  Group group_1 (
    .clk(clk), .in1(ram_1__1), .enable(en1), .stop(out_7), .in2(ram_1__2), .reset(HitBit), .MemRead(MemRead),
    .MemWrite(MemWrite), .in3(ram_1__3), .in4(ram_1__4), .Hit(Hit1), .out_12(group_1_out_12),
    .out_13(group_1_out_13), .out_14(group_1_out_14), .out_15(group_1_out_15), .in_10(Addr[11:6]));
  Group group_2 (
    .clk(clk), .in1(ram_1__1), .enable(en2), .stop(out_7), .in2(ram_1__2), .reset(HitBit), .MemRead(MemRead),
    .MemWrite(MemWrite), .in3(ram_1__3), .in4(ram_1__4), .Hit(Hit2), .out_12(group_2_out_12),
    .out_13(group_2_out_13), .out_14(group_2_out_14), .out_15(group_2_out_15), .in_10(Addr[11:6]));
  Group group_3 (
    .clk(clk), .in1(ram_1__1), .enable(en3), .stop(out_7), .in2(ram_1__2), .reset(HitBit), .MemRead(MemRead),
    .MemWrite(MemWrite), .in3(ram_1__3), .in4(ram_1__4), .Hit(Hit3), .out_12(group_3_out_12),
    .out_13(group_3_out_13), .out_14(group_3_out_14), .out_15(group_3_out_15), .in_10(Addr[11:6]));
  Group group_4 (
    .clk(clk), .in1(ram_1__1), .enable(en4), .stop(out_7), .in2(ram_1__2), .reset(HitBit), .MemRead(MemRead),
    .MemWrite(MemWrite), .in3(ram_1__3), .in4(ram_1__4), .Hit(Hit4), .out_12(group_4_out_12),
    .out_13(group_4_out_13), .out_14(group_4_out_14), .out_15(group_4_out_15), .in_10(Addr[11:6]));
  Multiplexer #(.select(2), .width(32), .enable("false")) multiplexer_1 (
    .in0(ram_1__1), .in1(ram_1__2), .in2(ram_1__3), .in3(ram_1__4), .out(multiplexer_1_out), .sel(Addr[3:2]));
  Multiplexer #(.select(2), .width(32), .enable("false")) multiplexer_2 (
    .in0(group_1_out_12), .in1(group_1_out_13), .in2(group_1_out_14), .in3(group_1_out_15),
    .out(multiplexer_2_out), .sel(Addr[3:2]));
  Multiplexer #(.select(2), .width(32), .enable("false")) multiplexer_3 (
    .in0(group_2_out_12), .in1(group_2_out_13), .in2(group_2_out_14), .in3(group_2_out_15),
    .out(multiplexer_3_out), .sel(Addr[3:2]));
  Multiplexer #(.select(2), .width(32), .enable("false")) multiplexer_4 (
    .in0(group_3_out_12), .in1(group_3_out_13), .in2(group_3_out_14), .in3(group_3_out_15),
    .out(multiplexer_4_out), .sel(Addr[3:2]));
  Multiplexer #(.select(2), .width(32), .enable("false")) multiplexer_5 (
    .in0(group_4_out_12), .in1(group_4_out_13), .in2(group_4_out_14), .in3(group_4_out_15),
    .out(multiplexer_5_out), .sel(Addr[3:2]));
  or or_2 (Hit, Hit1, Hit2, Hit3, Hit4);
  Multiplexer #(.select(2), .width(32), .enable("false")) multiplexer_6 (
    .in0(multiplexer_2_out), .in1(multiplexer_3_out), .in2(multiplexer_4_out), .in3(multiplexer_5_out),
    .out(multiplexer_6_out), .sel(Addr[5:4]));
  and and_7 (or_3_out[1], ~Hit, ~out_7, MemRead);  // AND_Gate
  Multiplexer #(.select(2), .width(32), .enable("false")) multiplexer_7 (
    .in0(multiplexer_6_out), .in1({32{1'b0}}), .in2(multiplexer_1_out), .in3({32{1'b0}}), .out(out_8),
    .sel(or_3_out));
  or or_3 (or_3_out[0], out_7, MemWrite);

  // Other names for the same wires on the sheet: MuxForBlock[1:0] = Addr[3:2]; MuxForGroup[1:0] = Addr[5:4];
  //   TAG[5:0] = Addr[11:6]; Data[31:0] = Data_in; reset = HitBit; stop = out_7
endmodule

module RAM (
  input  [1:0] MuxBlock,
  input  MemWrite,
  input  MemRead,
  input  Hit,
  input  [5:0] Tag,
  input  [1:0] MuxGroup,
  input  [31:0] MemData,
  input  Clk,
  input  Reset,
  output [31:0] _4,
  output [31:0] _3,
  output [31:0] _2,
  output out_13,
  output [31:0] _1
);

  wire _1_t, _2_t, _3_t, _4_t, and_1_out, and_2_out, counter_1_carry, not_1_out, not_2_out;
  wire [9:0] adder_1_out, adder_2_out, adder_3_out, adder_4_out, multiplexer_1_out;
  wire [31:0] ram_1_data, ram_2_data, ram_3_data, ram_4_data;

  and and_1 (and_1_out, MemRead, not_1_out);
  not not_1 (not_1_out, Hit);
  Counter_part #(.width(3), .max('h5)) counter_1 (
    .count(and_1_out), .carry(counter_1_carry), .clk(Clk), .clr(Reset));  // open: load, D, Q
  and and_2 (and_2_out, MemRead, Hit);
  and and_3 (out_13, and_1_out, not_2_out);
  not not_2 (not_2_out, counter_1_carry);
  Demultiplexer #(.select(2)) demultiplexer_1 (
    .out0(_1_t), .out1(_2_t), .out2(_3_t), .out3(_4_t), .in(MemWrite), .sel(MuxBlock));  // open: en
  Multiplexer #(.width(10), .enable("false")) multiplexer_1 (
    .in0({Tag, MuxGroup, 2'b00}), .in1({10{1'b0}}), .out(multiplexer_1_out), .sel(and_2_out));
  Adder #(.width(10)) adder_1 (.a(10'h3), .b(multiplexer_1_out), .out(adder_1_out));  // open: cin, cout
  Adder #(.width(10)) adder_2 (.a(10'h2), .b(multiplexer_1_out), .out(adder_2_out));  // open: cin, cout
  Adder #(.width(10)) adder_3 (.a(10'h1), .b(multiplexer_1_out), .out(adder_3_out));  // open: cin, cout
  Adder #(.width(10)) adder_4 (.a({10{1'b0}}), .b(multiplexer_1_out), .out(adder_4_out));  // open: cin, cout
  RAM_part #(.addrWidth(10), .dataWidth(32), .bus("separate")) ram_1 (
    .addr(adder_1_out), .din(MemData), .data(ram_1_data), .str(_4_t), .clk(Clk), .clr(Reset));  // open: sel, ld
  RAM_part #(.addrWidth(10), .dataWidth(32), .bus("separate")) ram_2 (
    .addr(adder_2_out), .din(MemData), .data(ram_2_data), .str(_3_t), .clk(Clk), .clr(Reset));  // open: sel, ld
  RAM_part #(.addrWidth(10), .dataWidth(32), .bus("separate")) ram_3 (
    .addr(adder_3_out), .din(MemData), .data(ram_3_data), .str(_2_t), .clk(Clk), .clr(Reset));  // open: sel, ld
  RAM_part #(.addrWidth(10), .dataWidth(32), .bus("separate")) ram_4 (
    .addr(adder_4_out), .din(MemData), .data(ram_4_data), .str(_1_t), .clk(Clk), .clr(Reset));  // open: sel, ld
  Multiplexer #(.width(32), .enable("false")) multiplexer_2 (.in0(ram_1_data), .in1(MemData), .out(_4), .sel(_4_t));
  Multiplexer #(.width(32), .enable("false")) multiplexer_3 (.in0(ram_2_data), .in1(MemData), .out(_3), .sel(_3_t));
  Multiplexer #(.width(32), .enable("false")) multiplexer_4 (.in0(ram_3_data), .in1(MemData), .out(_2), .sel(_2_t));
  Multiplexer #(.width(32), .enable("false")) multiplexer_5 (.in0(ram_4_data), .in1(MemData), .out(_1), .sel(_1_t));

  // Other names for the same wires on the sheet: Data[31:0] = MemData
endmodule

module LRU (
  input  [15:0] count1,
  input  [15:0] count2,
  input  [15:0] count3,
  input  [15:0] count4,
  input  hit1,
  input  hit2,
  input  hit3,
  input  hit4,
  input  memread,
  input  memwrite,
  input  enable,
  output out_12,
  output out_13,
  output out_14,
  output out_15
);

  wire and_1_out, and_2_out, and_3_out, and_4_out, and_5_out, comparator_1_lt, comparator_2_lt,
       comparator_3_lt, decoder_1_out0, decoder_1_out1, decoder_1_out2, decoder_1_out3, multiplexer_6_out,
       multiplexer_7_out, multiplexer_8_out, multiplexer_9_out, nor_1_out, not_1_out, or_1_out, or_2_out,
       or_3_out, or_4_out;
  wire [1:0] multiplexer_2_out, multiplexer_4_out, multiplexer_5_out;
  wire [15:0] multiplexer_1_out, multiplexer_3_out;

  Comparator #(.width(16), .mode("unsigned")) comparator_1 (
    .a(count1), .b(count2), .lt(comparator_1_lt));  // open: gt, eq
  Comparator #(.width(16), .mode("unsigned")) comparator_2 (
    .a(count3), .b(count4), .lt(comparator_2_lt));  // open: gt, eq
  Multiplexer #(.width(16), .enable("false")) multiplexer_1 (
    .in0(count1), .in1(count2), .out(multiplexer_1_out), .sel(comparator_1_lt));
  Multiplexer #(.width(2), .enable("false")) multiplexer_2 (
    .in0(2'b00), .in1(2'b01), .out(multiplexer_2_out), .sel(comparator_1_lt));
  Multiplexer #(.width(16), .enable("false")) multiplexer_3 (
    .in0(count3), .in1(count4), .out(multiplexer_3_out), .sel(comparator_2_lt));
  Multiplexer #(.width(2), .enable("false")) multiplexer_4 (
    .in0(2'b10), .in1(2'b11), .out(multiplexer_4_out), .sel(comparator_2_lt));
  Comparator #(.width(16), .mode("unsigned")) comparator_3 (
    .a(multiplexer_1_out), .b(multiplexer_3_out), .lt(comparator_3_lt));  // open: gt, eq
  Multiplexer #(.width(2), .enable("false")) multiplexer_5 (
    .in0(multiplexer_2_out), .in1(multiplexer_4_out), .out(multiplexer_5_out), .sel(comparator_3_lt));
  Decoder #(.select(2)) decoder_1 (
    .out0(decoder_1_out0), .out1(decoder_1_out1), .out2(decoder_1_out2), .out3(decoder_1_out3),
    .sel(multiplexer_5_out));  // open: en
  nor nor_1 (nor_1_out, hit1, hit2, hit3, hit4);
  and and_1 (and_1_out, nor_1_out, not_1_out);
  not not_1 (not_1_out, memwrite);
  Multiplexer #(.enable("false")) multiplexer_6 (
    .in0(1'b0), .in1(decoder_1_out0), .out(multiplexer_6_out), .sel(and_1_out));
  Multiplexer #(.enable("false")) multiplexer_7 (
    .in0(1'b0), .in1(decoder_1_out1), .out(multiplexer_7_out), .sel(and_1_out));
  Multiplexer #(.enable("false")) multiplexer_8 (
    .in0(1'b0), .in1(decoder_1_out2), .out(multiplexer_8_out), .sel(and_1_out));
  Multiplexer #(.enable("false")) multiplexer_9 (
    .in0(1'b0), .in1(decoder_1_out3), .out(multiplexer_9_out), .sel(and_1_out));
  and and_2 (and_2_out, hit1, memwrite);
  and and_3 (and_3_out, hit2, memwrite);
  and and_4 (and_4_out, hit3, memwrite);
  and and_5 (and_5_out, hit4, memwrite);
  or or_1 (or_1_out, multiplexer_6_out, and_2_out);
  or or_2 (or_2_out, multiplexer_7_out, and_3_out);
  or or_3 (or_3_out, multiplexer_8_out, and_4_out);
  or or_4 (or_4_out, multiplexer_9_out, and_5_out);
  and and_6 (out_12, enable, or_1_out);
  and and_7 (out_13, enable, or_2_out);
  and and_8 (out_14, enable, or_3_out);
  and and_9 (out_15, enable, or_4_out);
endmodule

module Block (
  input  [31:0] Block1_in,
  input  [31:0] Block2_in,
  input  [31:0] Block3_in,
  input  [5:0] tag_in,
  input  [31:0] Block4_in,
  input  clk,
  input  reset,
  input  enable,
  output [31:0] Block1_out,
  output [31:0] Block2_out,
  output [31:0] Block3_out,
  output [5:0] tag_out,
  output V,
  output [31:0] Block4_out
);

  Register #(.width(1)) register_1 (.D(1'b1), .en(enable), .Q(V), .clk(clk), .clr(reset));
  Register #(.width(6)) register_2 (.D(tag_in), .en(enable), .Q(tag_out), .clk(clk), .clr(reset));
  Register #(.width(32)) register_3 (.D(Block1_in), .en(enable), .Q(Block1_out), .clk(clk), .clr(reset));
  Register #(.width(32)) register_4 (.D(Block2_in), .en(enable), .Q(Block2_out), .clk(clk), .clr(reset));
  Register #(.width(32)) register_5 (.D(Block3_in), .en(enable), .Q(Block3_out), .clk(clk), .clr(reset));
  Register #(.width(32)) register_6 (.D(Block4_in), .en(enable), .Q(Block4_out), .clk(clk), .clr(reset));
endmodule

module Group (
  input  clk,
  input  [31:0] in1,
  input  enable,
  input  stop,
  input  [31:0] in2,
  input  reset,
  input  MemRead,
  input  MemWrite,
  input  [31:0] in3,
  input  [5:0] in_10,
  input  [31:0] in4,
  output [31:0] out_12,
  output [31:0] out_13,
  output [31:0] out_14,
  output [31:0] out_15,
  output Hit
);

  wire comparator_1_eq, comparator_2_eq, comparator_3_eq, comparator_4_eq, en, lru_1_out_12, lru_1_out_13,
       lru_1_out_14, lru_1_out_15, or_1_out, v1, v2, v3, v4;
  wire [1:0] bitfinder_1_index;
  wire [3:0] and_2_out;
  wire [5:0] tag1, tag2, tag3, tag4;
  wire [15:0] counter_1_count, counter_2_count, counter_3_count, counter_4_count;
  wire [31:0] _11, _12, _13, _14, _21, _22, _23, _24, _31, _32, _33, _34, _41, _42, _43, _44;

  Comparator #(.width(6), .mode("unsigned")) comparator_1 (.a(in_10), .b(tag1), .eq(comparator_1_eq));  // open: gt, lt
  Comparator #(.width(6), .mode("unsigned")) comparator_2 (.a(in_10), .b(tag2), .eq(comparator_2_eq));  // open: gt, lt
  Comparator #(.width(6), .mode("unsigned")) comparator_3 (.a(in_10), .b(tag3), .eq(comparator_3_eq));  // open: gt, lt
  Comparator #(.width(6), .mode("unsigned")) comparator_4 (.a(in_10), .b(tag4), .eq(comparator_4_eq));  // open: gt, lt
  and and_1 (en, enable, ~stop);  // AND_Gate
  and and_2 (and_2_out[0], comparator_1_eq, enable, v1);
  and and_3 (and_2_out[1], comparator_2_eq, enable, v2);
  and and_4 (and_2_out[2], comparator_3_eq, enable, v3);
  and and_5 (and_2_out[3], comparator_4_eq, enable, v4);
  or or_1 (or_1_out, and_2_out[3], and_2_out[2], and_2_out[1], and_2_out[0]);
  BitFinder #(.width(4)) bitfinder_1 (.in(and_2_out), .index(bitfinder_1_index));  // open: found
  and and_6 (Hit, or_1_out, enable);
  Counter counter_1 (
    .Enable(en), .Count(counter_1_count), .Hit(and_2_out[0]), .MemRead(MemRead), .Clk(clk), .Reset(reset),
    .Update(lru_1_out_12));
  Counter counter_2 (
    .Enable(en), .Count(counter_2_count), .Hit(and_2_out[1]), .MemRead(MemRead), .Clk(clk), .Reset(reset),
    .Update(lru_1_out_13));
  Counter counter_3 (
    .Enable(en), .Count(counter_3_count), .Hit(and_2_out[2]), .MemRead(MemRead), .Clk(clk), .Reset(reset),
    .Update(lru_1_out_14));
  Counter counter_4 (
    .Enable(en), .Count(counter_4_count), .Hit(and_2_out[3]), .MemRead(MemRead), .Clk(clk), .Reset(reset),
    .Update(lru_1_out_15));
  LRU lru_1 (
    .count1(counter_1_count), .count2(counter_2_count), .count3(counter_3_count), .count4(counter_4_count),
    .hit1(and_2_out[0]), .hit2(and_2_out[1]), .hit3(and_2_out[2]), .hit4(and_2_out[3]), .memread(MemRead),
    .memwrite(MemWrite), .enable(en), .out_12(lru_1_out_12), .out_13(lru_1_out_13), .out_14(lru_1_out_14),
    .out_15(lru_1_out_15));
  Block block_1 (
    .Block1_in(in1), .Block2_in(in2), .Block3_in(in3), .tag_in(in_10), .Block4_in(in4), .clk(clk),
    .reset(reset), .enable(lru_1_out_12), .tag_out(tag1), .V(v1), .Block1_out(_11), .Block2_out(_12),
    .Block3_out(_13), .Block4_out(_14));
  Block block_2 (
    .Block1_in(in1), .Block2_in(in2), .Block3_in(in3), .tag_in(in_10), .Block4_in(in4), .clk(clk),
    .reset(reset), .enable(lru_1_out_13), .tag_out(tag2), .V(v2), .Block1_out(_21), .Block2_out(_22),
    .Block3_out(_23), .Block4_out(_24));
  Block block_3 (
    .Block1_in(in1), .Block2_in(in2), .Block3_in(in3), .tag_in(in_10), .Block4_in(in4), .clk(clk),
    .reset(reset), .enable(lru_1_out_14), .tag_out(tag3), .V(v3), .Block1_out(_31), .Block2_out(_32),
    .Block3_out(_33), .Block4_out(_34));
  Block block_4 (
    .Block1_in(in1), .Block2_in(in2), .Block3_in(in3), .tag_in(in_10), .Block4_in(in4), .clk(clk),
    .reset(reset), .enable(lru_1_out_15), .tag_out(tag4), .V(v4), .Block1_out(_41), .Block2_out(_42),
    .Block3_out(_43), .Block4_out(_44));
  Multiplexer #(.select(2), .width(32), .enable("false")) multiplexer_1 (
    .in0(_11), .in1(_21), .in2(_31), .in3(_41), .out(out_12), .sel(bitfinder_1_index));
  Multiplexer #(.select(2), .width(32), .enable("false")) multiplexer_2 (
    .in0(_12), .in1(_22), .in2(_32), .in3(_42), .out(out_13), .sel(bitfinder_1_index));
  Multiplexer #(.select(2), .width(32), .enable("false")) multiplexer_3 (
    .in0(_13), .in1(_23), .in2(_33), .in3(_43), .out(out_14), .sel(bitfinder_1_index));
  Multiplexer #(.select(2), .width(32), .enable("false")) multiplexer_4 (
    .in0(_14), .in1(_24), .in2(_34), .in3(_44), .out(out_15), .sel(bitfinder_1_index));

  // Other names for the same wires on the sheet: tag[5:0] = in_10
endmodule

module Counter (
  input  Enable,
  input  Hit,
  input  MemRead,
  input  Clk,
  input  Reset,
  input  Update,
  output [15:0] Count
);

  wire and_1_out, and_2_out, and_3_out, and_4_out, or_1_out;

  and and_1 (and_1_out, Hit, MemRead);
  and and_2 (and_2_out, ~Hit, MemRead, Update);  // AND_Gate
  or or_1 (or_1_out, and_1_out, and_2_out);
  and and_3 (and_3_out, Enable, or_1_out);
  and and_4 (and_4_out, Enable, MemRead, ~or_1_out);  // AND_Gate
  Counter_part #(.width(16), .max('hffff)) counter_1 (
    .load(and_3_out), .D({16{1'b0}}), .count(and_4_out), .Q(Count), .clk(Clk), .clr(Reset));  // open: carry
endmodule
