// Logisim project pipeline CPU.circ as structural Verilog: 21 circuits, main circuit main
module main (
  input  remake,
  output [31:0] out_2,
  output out_3,
  output [4:0] out_4,
  output [31:0] out_5,
  output out_6,
  output [4:0] out_7,
  output [31:0] out_8
);

  wire B_beq, B_j, B_jal, clk, comparator_1_eq, controller_1_alusrc, controller_1_memwrite, controller_1_rw,
       ex_mem_1_out_15, ex_mem_1_out_16, fRtMsel, id_ex_1_out_21, id_ex_1_out_23, id_ex_1_out_25, stallD,
       stallE, stallF;
  wire [1:0] controller_1_dmop, controller_1_memtoreg, controller_1_regaddr, d_1_tuse1_d, d_1_tuse2_d,
       ex_mem_1_out_17, ex_mem_1_out_18, EXTop, fRsDsel, fRsEsel, fRtDsel, fRtEsel, id_ex_1_out_22,
       id_ex_1_out_26, id_ex_1_out_27, mem_wb_1_out_18;
  wire [2:0] NPCop;
  wire [3:0] controller_1_alucontrol, e_1_tnew_e, ex_mem_1_tnew_m, id_ex_1_out_24, mem_wb_1_tnew_w;
  wire [4:0] bit_extender_1_out, d_1_s1_d, d_1_s2_d, e_1_des_e, e_1_s1_e, e_1_s2_e, ex_mem_1_out_21,
       id_ex_1_rd_o, id_ex_1_rt_o, m_1_des_e, m_1_s2_m, multiplexer_6_out, splitter_1__11_15,
       splitter_1__16_20, splitter_1__21_25, w_1_des_e;
  wire [15:0] splitter_1__0_15;
  wire [23:0] pc_1_out_5;
  wire [31:0] aluresult_M, aluresult_W, dm_1_memoutdata, etod, ex_mem_1_pc_4_o, ex_mem_1_pc_o, EXT,
       ext_1_out_3, id_ex_1_pc_4_o, id_ex_1_pc_o, if_id_1_pc_4_o, if_id_1_pc_8_o, if_id_1_pc_o, Instr_D,
       Instr_E, Instr_M, instr_W, MemAddr_W, mtod, multiplexer_7_out, npc_1_npc, PC8_E, PC8_M, pc_1_out_6,
       pc_8_W, RD1, RD1_D, RD1_E, RD1_e_t, RD2, RD2_D, RD2_E, RD2_e_t, RD2_M, RD2_m_t, ReadData_W, Res, wtod;

  PC pc_1 (.in_3(npc_1_npc), .out_5(pc_1_out_5), .out_6(pc_1_out_6), .in_1(clk), .in_2(remake), .stallF(stallF));
  // Probe on npc_1_npc
  // Probe on fRsDsel
  // Probe on fRsEsel
  // Probe on fRtMsel
  // Probe on out_4
  // Probe on out_5
  // Probe on out_7
  // Probe on out_8
  // Probe on RD1_D
  Multiplexer #(.select(2), .width(32), .enable("false")) multiplexer_1 (
    .in0(RD1), .in1(etod), .in2(mtod), .in3({32{1'b0}}), .out(RD1_D), .sel(fRsDsel));
  // Probe on RD1_E
  Multiplexer #(.select(2), .width(32), .enable("false")) multiplexer_2 (
    .in0(RD1_e_t), .in1(mtod), .in2(wtod), .in3({32{1'b0}}), .out(RD1_E), .sel(fRsEsel));
  // Probe on RD2_m_t
  Multiplexer #(.width(32), .enable("false")) multiplexer_3 (.in0(RD2_M), .in1(wtod), .out(RD2_m_t), .sel(fRtMsel));
  Clock u_clk (.out(clk));
  ROM #(.addrWidth(24), .dataWidth(32)) rom_1 (.addr(pc_1_out_5), .data(out_2));  // open: sel
  // Probe on RD2_D
  // Probe on fRtDsel
  Multiplexer #(.select(2), .width(32), .enable("false")) multiplexer_4 (
    .in0(RD2), .in1(etod), .in2(mtod), .in3({32{1'b0}}), .out(RD2_D), .sel(fRtDsel));
  // Probe on RD2_E
  // Probe on fRtEsel
  Multiplexer #(.select(2), .width(32), .enable("false")) multiplexer_5 (
    .in0(RD2_e_t), .in1(mtod), .in2(wtod), .in3({32{1'b0}}), .out(RD2_E), .sel(fRtEsel));
  // Probe on Instr_D
  IF_ID if_id_1 (
    .instr_i(out_2), .pc_i(pc_1_out_6), .instr_o(Instr_D), .pc_o(if_id_1_pc_o), .pc_4_o(if_id_1_pc_4_o),
    .pc_8_o(if_id_1_pc_8_o), .in_1(clk), .in_2(remake), .in_5(stallD));
  Comparator #(.width(32), .mode("unsigned")) comparator_1 (
    .a(RD1_D), .b(RD2_D), .eq(comparator_1_eq));  // open: gt, lt
  NPC npc_1 (
    .pc(pc_1_out_6), .instr(Instr_D), .extresult(EXT), .RD1(RD1_D), .npc(npc_1_npc), .zero(comparator_1_eq),
    .jr(B_jal), .j_jal(B_j), .beq(B_beq));
  // Probe on Instr_D
  // Probe on etod
  Controller controller_1 (
    .RW(controller_1_rw), .B_beq(B_beq), .B_j(B_j), .B_jr(B_jal), .RegAddr(controller_1_regaddr),
    .ALUSrc(controller_1_alusrc), .ALUControl(controller_1_alucontrol), .MemWrite(controller_1_memwrite),
    .MemtoReg(controller_1_memtoreg), .EXTOp(EXTop), .DMOp(controller_1_dmop), .Instr(Instr_D));
  Splitter splitter_1 (
    .INPUT(Instr_D), ._21_25(splitter_1__21_25), ._16_20(splitter_1__16_20), ._11_15(splitter_1__11_15),
    ._0_15(splitter_1__0_15));  // open: _0_25
  // Probe on Instr_E
  // Probe on mtod
  D d_1 (.Instr(Instr_D), .S1_D(d_1_s1_d), .S2_D(d_1_s2_d), .tuse1_D(d_1_tuse1_d), .tuse2_D(d_1_tuse2_d));
  E e_1 (
    .Instr(Instr_E), .extendresult(EXT), .pc_8(PC8_E), .S1_E(e_1_s1_e), .S2_E(e_1_s2_e), .tnew_E(e_1_tnew_e),
    .Des_E(e_1_des_e), .etod(etod));
  M m_1 (
    .Instr(Instr_M), .pc_8(PC8_M), .aluresult(aluresult_M), .S2_M(m_1_s2_m), .Des_E(m_1_des_e), .mtod(mtod));  // open: S1_M
  W w_1 (.Instr(instr_W), .aluresult(aluresult_W), .pc_8(pc_8_W), .regdata(out_5), .Des_E(w_1_des_e), .wtod(wtod));
  // Probe on wtod
  // Probe on d_1_s1_d
  // Probe on d_1_s2_d
  stallUnit stallunit_1 (
    .s1_D(d_1_s1_d), .s2_D(d_1_s2_d), .tUse1_D(d_1_tuse1_d), .tUse2_D(d_1_tuse2_d), .des_E(e_1_des_e),
    .tNew_E(e_1_tnew_e), .tNew_M(ex_mem_1_tnew_m), .des_M(m_1_des_e), .Stall_F(stallF), .Stall_D(stallD),
    .flush_E(stallE));
  // Probe on Instr_M
  npcop npcop_1 (.beq(B_beq), .jal(B_j), .jr(B_jal), .NPCop(NPCop));
  GRF grf_1 (
    .A1(splitter_1__21_25), .A2(splitter_1__16_20), .A3(out_4), .WD(out_5), .RD1(RD1), .RD2(RD2), .clk(clk),
    .reset(remake), .we(out_3));
  EXT ext_1 (.in_2(splitter_1__0_15), .out_3(ext_1_out_3), .in_1(EXTop));
  // Probe on d_1_tuse1_d
  // Probe on instr_W
  // Probe on e_1_des_e
  // Probe on d_1_tuse2_d
  // Probe on e_1_tnew_e
  // Probe on Res
  // Probe on Res
  // Probe on RD2_m_t
  // Probe on RD1_D
  // Probe on RD2_D
  // Probe on id_ex_1_out_22
  // Probe on id_ex_1_out_24
  ID_EX id_ex_1 (
    .pc_i(if_id_1_pc_o), .RD1_i(RD1_D), .pc_4_i(if_id_1_pc_4_o), .RD2_i(RD2_D), .pc_8_i(if_id_1_pc_8_o),
    .rs_i(splitter_1__21_25), .rt_i(splitter_1__16_20), .rd_i(splitter_1__11_15), .instr_i(Instr_D),
    .pc_o(id_ex_1_pc_o), .RD1_o(RD1_e_t), .pc_4_o(id_ex_1_pc_4_o), .RD2_o(RD2_e_t), .pc_8_o(PC8_E),
    .rt_o(id_ex_1_rt_o), .rd_o(id_ex_1_rd_o), .out_37(Instr_E), .in_1(clk), .in_2(remake), .in_19(stallE),
    .regaddr(controller_1_regaddr), .out_22(id_ex_1_out_22), .out_25(id_ex_1_out_25),
    .memwrite(controller_1_memwrite), .regwrite(controller_1_rw), .out_21(id_ex_1_out_21),
    .alusrc(controller_1_alusrc), .out_23(id_ex_1_out_23), .memtoreg(controller_1_memtoreg),
    .out_26(id_ex_1_out_26), .out_24(id_ex_1_out_24), .aluctrl(controller_1_alucontrol),
    .DMop(controller_1_dmop), .out_27(id_ex_1_out_27), .out_36(EXT), .EXTresult(ext_1_out_3));  // open: rs_o
  // Probe on ex_mem_1_tnew_m
  // Probe on m_1_des_e
  // Probe on d_1_s1_d
  // Probe on d_1_s2_d
  forwardUnit forwardunit_1 (
    .s1_D(d_1_s1_d), .s2_D(d_1_s2_d), .s1_E(e_1_s1_e), .s2_E(e_1_s2_e), .des_E(e_1_des_e),
    .tNew_E(e_1_tnew_e), .s2_M(m_1_s2_m), .tNew_M(ex_mem_1_tnew_m), .des_M(m_1_des_e),
    .tNew_W(mem_wb_1_tnew_w), .des_W(w_1_des_e), .fRsDsel(fRsDsel), .fRtDsel(fRtDsel), .fRsEsel(fRsEsel),
    .fRtEsel(fRtEsel), .fRtMsel(fRtMsel));
  // Probe on out_5
  Multiplexer #(.select(2), .width(5), .enable("false")) multiplexer_6 (
    .in0(id_ex_1_rt_o), .in1(id_ex_1_rd_o), .in2({5{1'b1}}), .out(multiplexer_6_out), .sel(id_ex_1_out_22));  // open: in3
  // Probe on e_1_s1_e
  Multiplexer #(.width(32), .enable("false")) multiplexer_7 (
    .in0(RD2_E), .in1(EXT), .out(multiplexer_7_out), .sel(id_ex_1_out_23));
  Bit_Extender #(.in_width(32), .out_width(5)) bit_extender_1 (.in(EXT), .out(bit_extender_1_out));
  // Probe on e_1_s2_e
  // Probe on e_1_des_e
  ALU alu_1 (
    .ALUControl(id_ex_1_out_24), .RD1(RD1_E), .RD2(multiplexer_7_out), .ALUresult(Res),
    .shamt(bit_extender_1_out));
  // Probe on e_1_tnew_e
  // Probe on ex_mem_1_tnew_m
  // Probe on m_1_s2_m
  // Probe on m_1_des_e
  // Probe on mem_wb_1_tnew_w
  EX_MEM ex_mem_1 (
    .memwrite(id_ex_1_out_25), .regwrite(id_ex_1_out_21), .memtoreg(id_ex_1_out_26), .DMop(id_ex_1_out_27),
    .aluresult_i(Res), .writedata_i(RD2_E), .writereg_i(multiplexer_6_out), .pc_i(id_ex_1_pc_o),
    .pc_4_i(id_ex_1_pc_4_o), .pc_8_i(PC8_E), .instr_i(Instr_E), .out_16(ex_mem_1_out_16),
    .out_15(ex_mem_1_out_15), .out_17(ex_mem_1_out_17), .out_18(ex_mem_1_out_18), .out_19(aluresult_M),
    .out_20(RD2_M), .out_21(ex_mem_1_out_21), .pc_o(ex_mem_1_pc_o), .pc_4_o(ex_mem_1_pc_4_o), .pc_8_o(PC8_M),
    .out_25(Instr_M), .in_1(clk), .in_2(remake), .tnew_E(e_1_tnew_e), .tnew_M(ex_mem_1_tnew_m));
  // Probe on w_1_des_e
  DM dm_1 (
    .ALUresult(aluresult_M), .MemWriteData(RD2_m_t), .MemOutData(dm_1_memoutdata), .in_1(clk), .in_2(remake),
    .in_3(ex_mem_1_out_16), .DMOp(ex_mem_1_out_18));
  MEM_WB mem_wb_1 (
    .regwrite(ex_mem_1_out_15), .memtoreg(ex_mem_1_out_17), .writereg_i(ex_mem_1_out_21),
    .aluresult_i(aluresult_M), .readdata_i(dm_1_memoutdata), .pc_i(ex_mem_1_pc_o), .pc_4_i(ex_mem_1_pc_4_o),
    .pc_8_i(PC8_M), .instr_i(Instr_M), .memaddr(aluresult_M), .memdata(RD2_m_t), .memwrite(ex_mem_1_out_16),
    .out_17(out_3), .out_18(mem_wb_1_out_18), .out_19(out_4), .out_20(aluresult_W), .out_22(ReadData_W),
    .pc_8_o(pc_8_W), .out_26(instr_W), .out_27({MemAddr_W[31:7], out_7, MemAddr_W[1:0]}), .out_28(out_8),
    .out_29(out_6), .in_1(clk), .in_2(remake), .tnew_M(ex_mem_1_tnew_m), .tnew_W(mem_wb_1_tnew_w));  // open: writedata_i, out_21, pc_o, pc_4_o
  Multiplexer #(.select(2), .width(32), .enable("false")) multiplexer_8 (
    .in0(aluresult_W), .in1(ReadData_W), .in2(pc_8_W), .out(out_5), .sel(mem_wb_1_out_18));  // open: in3

  // Other names for the same wires on the sheet: Instr[31:0] = out_2; MemAddr_W[6:2] = out_7; MemData_W[31:0] = out_8;
  //   MemWrite_W = out_6; RegAddr_W[4:0] = out_4; RegData_W[31:0] = out_5; RegWrite_W = out_3

  // Notes on the sheet:
  //   contents of rom_1 (hex, n*v repeats v):
  //   35080001 35290000 356b7fff 356cffff 35080002 3529ffff 1085021 1295821 35080002 3529ffff 1085023
  //   1295823 1286023 1096023 3c087fff 3508777f 35080004 1084821 1095023 14a5821 10b6023 ad8c0010 ad2bfffc
  //   8d8d0010 8d2efffc
endmodule

module forwardUnit (
  input  [4:0] s1_D,
  input  [4:0] s2_D,
  input  [4:0] s1_E,
  input  [4:0] s2_E,
  input  [4:0] des_E,
  input  [3:0] tNew_E,
  input  [4:0] s2_M,
  input  [3:0] tNew_M,
  input  [4:0] des_M,
  input  [3:0] tNew_W,
  input  [4:0] des_W,
  output [1:0] fRsDsel,
  output [1:0] fRtDsel,
  output [1:0] fRsEsel,
  output [1:0] fRtEsel,
  output fRtMsel
);

  wire and_1_out, and_2_out, and_3_out, and_4_out, and_5_out, and_6_out, and_7_out, and_8_out, and_9_out,
       comparator_1_eq, comparator_2_eq, comparator_3_eq, comparator_4_eq, comparator_5_eq, comparator_6_eq,
       comparator_7_eq, comparator_8_eq, comparator_9_eq, comparator_10_eq, comparator_11_eq,
       comparator_12_eq, comparator_13_eq, comparator_14_eq, comparator_15_eq, comparator_16_eq,
       comparator_17_eq, comparator_18_eq, comparator_19_eq, comparator_20_eq, comparator_21_eq,
       comparator_22_eq, comparator_23_eq, comparator_24_eq, comparator_25_eq, comparator_26_eq,
       comparator_27_eq, not_1_out, not_2_out, not_3_out, not_4_out, not_5_out, not_6_out, not_7_out,
       not_8_out, not_9_out;
  wire [1:0] multiplexer_1_out, multiplexer_2_out, multiplexer_5_out, multiplexer_6_out;

  Comparator #(.width(5), .mode("unsigned")) comparator_1 (
    .a(s1_D), .b({5{1'b0}}), .eq(comparator_1_eq));  // open: gt, lt
  not not_1 (not_1_out, comparator_1_eq);
  Comparator #(.width(5), .mode("unsigned")) comparator_2 (.a(s1_D), .b(des_M), .eq(comparator_2_eq));  // open: gt, lt
  Comparator #(.width(4), .mode("unsigned")) comparator_3 (
    .a(tNew_M), .b(4'b0000), .eq(comparator_3_eq));  // open: gt, lt
  not not_2 (not_2_out, comparator_4_eq);
  Comparator #(.width(5), .mode("unsigned")) comparator_4 (
    .a(s1_D), .b({5{1'b0}}), .eq(comparator_4_eq));  // open: gt, lt
  Comparator #(.width(5), .mode("unsigned")) comparator_5 (.a(s1_D), .b(des_E), .eq(comparator_5_eq));  // open: gt, lt
  Comparator #(.width(4), .mode("unsigned")) comparator_6 (
    .a(tNew_E), .b(4'b0000), .eq(comparator_6_eq));  // open: gt, lt
  Comparator #(.width(5), .mode("unsigned")) comparator_7 (
    .a(s2_D), .b({5{1'b0}}), .eq(comparator_7_eq));  // open: gt, lt
  Comparator #(.width(5), .mode("unsigned")) comparator_8 (.a(s2_D), .b(des_M), .eq(comparator_8_eq));  // open: gt, lt
  Comparator #(.width(4), .mode("unsigned")) comparator_9 (
    .a(tNew_M), .b(4'b0000), .eq(comparator_9_eq));  // open: gt, lt
  Comparator #(.width(5), .mode("unsigned")) comparator_10 (
    .a(s2_D), .b({5{1'b0}}), .eq(comparator_10_eq));  // open: gt, lt
  Comparator #(.width(5), .mode("unsigned")) comparator_11 (
    .a(s2_D), .b(des_E), .eq(comparator_11_eq));  // open: gt, lt
  Comparator #(.width(4), .mode("unsigned")) comparator_12 (
    .a(tNew_E), .b(4'b0000), .eq(comparator_12_eq));  // open: gt, lt
  and and_1 (and_1_out, not_1_out, comparator_2_eq, comparator_3_eq);
  and and_2 (and_2_out, not_2_out, comparator_5_eq, comparator_6_eq);
  not not_3 (not_3_out, comparator_7_eq);
  not not_4 (not_4_out, comparator_10_eq);
  Multiplexer #(.width(2)) multiplexer_1 (
    .in0(2'b00), .in1(2'b10), .out(multiplexer_1_out), .sel(and_1_out));  // open: en
  and and_3 (and_3_out, not_3_out, comparator_8_eq, comparator_9_eq);
  and and_4 (and_4_out, not_4_out, comparator_11_eq, comparator_12_eq);
  Multiplexer #(.width(2)) multiplexer_2 (
    .in0(2'b00), .in1(2'b10), .out(multiplexer_2_out), .sel(and_3_out));  // open: en
  Multiplexer #(.width(2)) multiplexer_3 (
    .in0(multiplexer_1_out), .in1(2'b01), .out(fRsDsel), .sel(and_2_out));  // open: en
  Multiplexer #(.width(2)) multiplexer_4 (
    .in0(multiplexer_2_out), .in1(2'b01), .out(fRtDsel), .sel(and_4_out));  // open: en
  Comparator #(.width(5), .mode("unsigned")) comparator_13 (
    .a(s1_E), .b({5{1'b0}}), .eq(comparator_13_eq));  // open: gt, lt
  Comparator #(.width(5), .mode("unsigned")) comparator_14 (
    .a(s1_E), .b(des_W), .eq(comparator_14_eq));  // open: gt, lt
  Comparator #(.width(4), .mode("unsigned")) comparator_15 (
    .a(tNew_W), .b(4'b0000), .eq(comparator_15_eq));  // open: gt, lt
  Comparator #(.width(5), .mode("unsigned")) comparator_16 (
    .a(s1_E), .b({5{1'b0}}), .eq(comparator_16_eq));  // open: gt, lt
  Comparator #(.width(5), .mode("unsigned")) comparator_17 (
    .a(s1_E), .b(des_M), .eq(comparator_17_eq));  // open: gt, lt
  Comparator #(.width(4), .mode("unsigned")) comparator_18 (
    .a(tNew_M), .b(4'b0000), .eq(comparator_18_eq));  // open: gt, lt
  Comparator #(.width(5), .mode("unsigned")) comparator_19 (
    .a(s2_E), .b({5{1'b0}}), .eq(comparator_19_eq));  // open: gt, lt
  Comparator #(.width(5), .mode("unsigned")) comparator_20 (
    .a(s2_E), .b(des_W), .eq(comparator_20_eq));  // open: gt, lt
  Comparator #(.width(4), .mode("unsigned")) comparator_21 (
    .a(tNew_W), .b(4'b0000), .eq(comparator_21_eq));  // open: gt, lt
  Comparator #(.width(5), .mode("unsigned")) comparator_22 (
    .a(s2_E), .b({5{1'b0}}), .eq(comparator_22_eq));  // open: gt, lt
  Comparator #(.width(5), .mode("unsigned")) comparator_23 (
    .a(s2_E), .b(des_M), .eq(comparator_23_eq));  // open: gt, lt
  Comparator #(.width(4), .mode("unsigned")) comparator_24 (
    .a(tNew_M), .b(4'b0000), .eq(comparator_24_eq));  // open: gt, lt
  not not_5 (not_5_out, comparator_13_eq);
  not not_6 (not_6_out, comparator_16_eq);
  not not_7 (not_7_out, comparator_19_eq);
  not not_8 (not_8_out, comparator_22_eq);
  and and_5 (and_5_out, not_5_out, comparator_14_eq, comparator_15_eq);
  and and_6 (and_6_out, not_6_out, comparator_17_eq, comparator_18_eq);
  and and_7 (and_7_out, not_7_out, comparator_20_eq, comparator_21_eq);
  and and_8 (and_8_out, not_8_out, comparator_23_eq, comparator_24_eq);
  Multiplexer #(.width(2)) multiplexer_5 (
    .in0(2'b00), .in1(2'b10), .out(multiplexer_5_out), .sel(and_5_out));  // open: en
  Multiplexer #(.width(2)) multiplexer_6 (
    .in0(2'b00), .in1(2'b10), .out(multiplexer_6_out), .sel(and_7_out));  // open: en
  Multiplexer #(.width(2)) multiplexer_7 (
    .in0(multiplexer_5_out), .in1(2'b01), .out(fRsEsel), .sel(and_6_out));  // open: en
  Multiplexer #(.width(2)) multiplexer_8 (
    .in0(multiplexer_6_out), .in1(2'b01), .out(fRtEsel), .sel(and_8_out));  // open: en
  Comparator #(.width(5), .mode("unsigned")) comparator_25 (
    .a(s2_M), .b({5{1'b0}}), .eq(comparator_25_eq));  // open: gt, lt
  not not_9 (not_9_out, comparator_25_eq);
  Comparator #(.width(5), .mode("unsigned")) comparator_26 (
    .a(s2_M), .b(des_W), .eq(comparator_26_eq));  // open: gt, lt
  Comparator #(.width(4), .mode("unsigned")) comparator_27 (
    .a(tNew_W), .b(4'b0000), .eq(comparator_27_eq));  // open: gt, lt
  and and_9 (and_9_out, not_9_out, comparator_26_eq, comparator_27_eq);
  Multiplexer multiplexer_9 (.in0(1'b0), .in1(1'b1), .out(fRtMsel), .sel(and_9_out));  // open: en
endmodule

module stallUnit (
  input  [4:0] s1_D,
  input  [4:0] s2_D,
  input  [1:0] tUse1_D,
  input  [1:0] tUse2_D,
  input  [4:0] des_E,
  input  [3:0] tNew_E,
  input  [3:0] tNew_M,
  input  [4:0] des_M,
  output Stall_F,
  output Stall_D,
  output flush_E
);

  wire and_1_out, and_2_out, and_3_out, and_4_out, comparator_1_eq, comparator_2_eq, comparator_3_lt,
       comparator_4_eq, comparator_5_eq, comparator_6_lt, comparator_7_eq, comparator_8_eq, comparator_9_lt,
       comparator_10_eq, comparator_11_eq, comparator_12_lt, not_1_out, not_2_out, not_3_out, not_4_out;
  wire [3:0] tUse1_D_t, tUse2_D_t;

  Comparator #(.width(5), .mode("unsigned")) comparator_1 (
    .a(s1_D), .b({5{1'b0}}), .eq(comparator_1_eq));  // open: gt, lt
  Comparator #(.width(5), .mode("unsigned")) comparator_2 (.a(s1_D), .b(des_E), .eq(comparator_2_eq));  // open: gt, lt
  Comparator #(.width(4), .mode("unsigned")) comparator_3 (
    .a(tUse1_D_t), .b(tNew_E), .lt(comparator_3_lt));  // open: gt, eq
  Comparator #(.width(5), .mode("unsigned")) comparator_4 (
    .a(s2_D), .b({5{1'b0}}), .eq(comparator_4_eq));  // open: gt, lt
  Comparator #(.width(5), .mode("unsigned")) comparator_5 (.a(s2_D), .b(des_E), .eq(comparator_5_eq));  // open: gt, lt
  Comparator #(.width(4), .mode("unsigned")) comparator_6 (
    .a(tUse2_D_t), .b(tNew_E), .lt(comparator_6_lt));  // open: gt, eq
  Comparator #(.width(5), .mode("unsigned")) comparator_7 (
    .a(s1_D), .b({5{1'b0}}), .eq(comparator_7_eq));  // open: gt, lt
  Comparator #(.width(5), .mode("unsigned")) comparator_8 (.a(s1_D), .b(des_M), .eq(comparator_8_eq));  // open: gt, lt
  Comparator #(.width(4), .mode("unsigned")) comparator_9 (
    .a(tUse1_D_t), .b(tNew_M), .lt(comparator_9_lt));  // open: gt, eq
  Comparator #(.width(5), .mode("unsigned")) comparator_10 (
    .a(s2_D), .b({5{1'b0}}), .eq(comparator_10_eq));  // open: gt, lt
  Comparator #(.width(5), .mode("unsigned")) comparator_11 (
    .a(s2_D), .b(des_M), .eq(comparator_11_eq));  // open: gt, lt
  Comparator #(.width(4), .mode("unsigned")) comparator_12 (
    .a(tUse2_D_t), .b(tNew_M), .lt(comparator_12_lt));  // open: gt, eq
  assign tUse1_D_t = {{2{1'b0}}, tUse1_D};  // Bit_Extender bit_extender_1
  not not_1 (not_1_out, comparator_1_eq);
  not not_2 (not_2_out, comparator_4_eq);
  not not_3 (not_3_out, comparator_7_eq);
  not not_4 (not_4_out, comparator_10_eq);
  and and_1 (and_1_out, not_1_out, comparator_2_eq, comparator_3_lt);
  and and_2 (and_2_out, not_2_out, comparator_5_eq, comparator_6_lt);
  and and_3 (and_3_out, not_3_out, comparator_8_eq, comparator_9_lt);
  and and_4 (and_4_out, not_4_out, comparator_11_eq, comparator_12_lt);
  assign tUse2_D_t = {{2{1'b0}}, tUse2_D};  // Bit_Extender bit_extender_2
  or or_1 (flush_E, and_1_out, and_2_out, and_3_out, and_4_out);

  assign Stall_D = flush_E;
  assign Stall_F = flush_E;

  // Other names for the same wires on the sheet: stall_flag = flush_E
endmodule

module PC (
  input  in_1,
  input  in_2,
  input  [31:0] in_3,
  input  stallF,
  output [23:0] out_5,
  output [31:0] out_6
);

  wire comparator_1_eq, not_1_out;
  wire [31:0] register_1_q, subtractor_1_out;

  not not_1 (not_1_out, stallF);
  Register #(.width(32)) register_1 (.D(in_3), .en(not_1_out), .Q(register_1_q), .clk(in_1), .clr(in_2));
  Comparator #(.width(32)) comparator_1 (.a(register_1_q), .b({32{1'b0}}), .eq(comparator_1_eq));  // open: gt, lt
  Multiplexer #(.width(32), .enable("false")) multiplexer_1 (
    .in0(register_1_q), .in1(32'h3000), .out(out_6), .sel(comparator_1_eq));
  Subtractor #(.width(32)) subtractor_1 (
    .a(out_6), .b(32'h3000), .out({subtractor_1_out[31:26], out_5, subtractor_1_out[1:0]}));  // open: bin, bout

  // Other names for the same wires on the sheet: clk = in_1; reset = in_2
endmodule

module IF_ID (
  input  in_1,
  input  in_2,
  input  [31:0] instr_i,
  input  [31:0] pc_i,
  input  in_5,
  output [31:0] instr_o,
  output [31:0] pc_o,
  output [31:0] pc_4_o,
  output [31:0] pc_8_o
);

  wire not_1_out, not_2_out;

  not not_1 (not_1_out, in_5);
  not not_2 (not_2_out, in_5);
  Register #(.width(32)) register_1 (.D(instr_i), .en(not_1_out), .Q(instr_o), .clk(in_1), .clr(in_2));
  Register #(.width(32)) register_2 (.D(pc_i), .en(not_2_out), .Q(pc_o), .clk(in_1), .clr(in_2));
  Adder #(.width(32)) adder_1 (.a(pc_o), .b(32'h4), .out(pc_4_o));  // open: cin, cout
  Adder #(.width(32)) adder_2 (.a(pc_4_o), .b(32'h4), .out(pc_8_o));  // open: cin, cout

  // Other names for the same wires on the sheet: clk = in_1; F_D_stall = in_5; reset = in_2
endmodule

module Splitter (
  input  [31:0] INPUT,
  output [4:0] _21_25,
  output [4:0] _16_20,
  output [4:0] _11_15,
  output [15:0] _0_15,
  output [25:0] _0_25
);


  assign _0_15 = INPUT[15:0];
  assign _0_25 = INPUT[25:0];
  assign _11_15 = INPUT[15:11];
  assign _16_20 = INPUT[20:16];
  assign _21_25 = INPUT[25:21];
endmodule

module GRF (
  input  [4:0] A1,
  input  clk,
  input  reset,
  input  we,
  input  [4:0] A2,
  input  [4:0] A3,
  input  [31:0] WD,
  output [31:0] RD1,
  output [31:0] RD2
);

  wire comparator_1_eq, comparator_2_eq, comparator_3_eq, comparator_4_eq;
  wire [31:0] I0, I1, I2, I3, I4, I5, I6, I7, I8, I9, I10, I11, I12, I13, I14, I15, I16, I17, I18, I19, I20,
       I21, I22, I23, I24, I25, I26, I27, I28, I29, I30, I31, multiplexer_2_out, multiplexer_3_out, O0, O1,
       O2, O3, O4, O5, O6, O7, O8, O9, O10, O11, O12, O13, O14, O15, O16, O17, O18, O19, O20, O21, O22, O23,
       O24, O25, O26, O27, O28, O29, O30, O31, RD1_t, RD2_t;

  // Probe on A3
  // Probe on WD
  Demultiplexer #(.select(5), .width(32), .tristate("true")) demultiplexer_1 (
    .out0(I0), .out1(I1), .out2(I2), .out3(I3), .out4(I4), .out5(I5), .out6(I6), .out7(I7), .out8(I8),
    .out9(I9), .out10(I10), .out11(I11), .out12(I12), .out13(I13), .out14(I14), .out15(I15), .out16(I16),
    .out17(I17), .out18(I18), .out19(I19), .out20(I20), .out21(I21), .out22(I22), .out23(I23), .out24(I24),
    .out25(I25), .out26(I26), .out27(I27), .out28(I28), .out29(I29), .out30(I30), .out31(I31), .in(WD),
    .sel(A3));  // open: en
  Multiplexer #(.select(5), .width(32)) multiplexer_1 (
    .in0(O0), .in1(O1), .in2(O2), .in3(O3), .in4(O4), .in5(O5), .in6(O6), .in7(O7), .in8(O8), .in9(O9),
    .in10(O10), .in11(O11), .in12(O12), .in13(O13), .in14(O14), .in15(O15), .in16(O16), .in17(O17),
    .in18(O18), .in19(O19), .in20(O20), .in21(O21), .in22(O22), .in23(O23), .in24(O24), .in25(O25),
    .in26(O26), .in27(O27), .in28(O28), .in29(O29), .in30(O30), .in31(O31), .out(RD2_t), .sel(A2));  // open: en
  Multiplexer #(.width(32), .enable("false")) multiplexer_2 (
    .in0(RD1_t), .in1(WD), .out(multiplexer_2_out), .sel(comparator_1_eq));
  Comparator #(.width(5), .mode("unsigned")) comparator_1 (.a(A1), .b(A3), .eq(comparator_1_eq));  // open: gt, lt
  Multiplexer #(.width(32), .enable("false")) multiplexer_3 (
    .in0(RD2_t), .in1(WD), .out(multiplexer_3_out), .sel(comparator_2_eq));
  Comparator #(.width(5), .mode("unsigned")) comparator_2 (.a(A2), .b(A3), .eq(comparator_2_eq));  // open: gt, lt
  Comparator #(.width(5), .mode("unsigned")) comparator_3 (
    .a(A1), .b({5{1'b0}}), .eq(comparator_3_eq));  // open: gt, lt
  Comparator #(.width(5), .mode("unsigned")) comparator_4 (
    .a(A2), .b({5{1'b0}}), .eq(comparator_4_eq));  // open: gt, lt
  Multiplexer #(.width(32), .enable("false")) multiplexer_4 (
    .in0(multiplexer_2_out), .in1({32{1'b0}}), .out(RD1), .sel(comparator_3_eq));
  Multiplexer #(.width(32), .enable("false")) multiplexer_5 (
    .in0(multiplexer_3_out), .in1({32{1'b0}}), .out(RD2), .sel(comparator_4_eq));
  Multiplexer #(.select(5), .width(32)) multiplexer_6 (
    .in0(O0), .in1(O1), .in2(O2), .in3(O3), .in4(O4), .in5(O5), .in6(O6), .in7(O7), .in8(O8), .in9(O9),
    .in10(O10), .in11(O11), .in12(O12), .in13(O13), .in14(O14), .in15(O15), .in16(O16), .in17(O17),
    .in18(O18), .in19(O19), .in20(O20), .in21(O21), .in22(O22), .in23(O23), .in24(O24), .in25(O25),
    .in26(O26), .in27(O27), .in28(O28), .in29(O29), .in30(O30), .in31(O31), .out(RD1_t), .sel(A1));  // open: en
  Register #(.width(32)) register_1 (.D({32{1'b0}}), .en(we), .Q(O0), .clk(clk), .clr(reset));
  Register #(.width(32)) register_2 (.D(I8), .en(we), .Q(O8), .clk(clk), .clr(reset));
  Register #(.width(32)) register_3 (.D(I16), .en(we), .Q(O16), .clk(clk), .clr(reset));
  Register #(.width(32)) register_4 (.D(I24), .en(we), .Q(O24), .clk(clk), .clr(reset));
  Register #(.width(32)) register_5 (.D(I1), .en(we), .Q(O1), .clk(clk), .clr(reset));
  Register #(.width(32)) register_6 (.D(I9), .en(we), .Q(O9), .clk(clk), .clr(reset));
  Register #(.width(32)) register_7 (.D(I17), .en(we), .Q(O17), .clk(clk), .clr(reset));
  Register #(.width(32)) register_8 (.D(I25), .en(we), .Q(O25), .clk(clk), .clr(reset));
  Register #(.width(32)) register_9 (.D(I2), .en(we), .Q(O2), .clk(clk), .clr(reset));
  Register #(.width(32)) register_10 (.D(I10), .en(we), .Q(O10), .clk(clk), .clr(reset));
  Register #(.width(32)) register_11 (.D(I18), .en(we), .Q(O18), .clk(clk), .clr(reset));
  Register #(.width(32)) register_12 (.D(I26), .en(we), .Q(O26), .clk(clk), .clr(reset));
  Register #(.width(32)) register_13 (.D(I3), .en(we), .Q(O3), .clk(clk), .clr(reset));
  Register #(.width(32)) register_14 (.D(I11), .en(we), .Q(O11), .clk(clk), .clr(reset));
  Register #(.width(32)) register_15 (.D(I19), .en(we), .Q(O19), .clk(clk), .clr(reset));
  Register #(.width(32)) register_16 (.D(I27), .en(we), .Q(O27), .clk(clk), .clr(reset));
  Register #(.width(32)) register_17 (.D(I4), .en(we), .Q(O4), .clk(clk), .clr(reset));
  Register #(.width(32)) register_18 (.D(I12), .en(we), .Q(O12), .clk(clk), .clr(reset));
  Register #(.width(32)) register_19 (.D(I20), .en(we), .Q(O20), .clk(clk), .clr(reset));
  Register #(.width(32)) register_20 (.D(I28), .en(we), .Q(O28), .clk(clk), .clr(reset));
  Register #(.width(32)) register_21 (.D(I5), .en(we), .Q(O5), .clk(clk), .clr(reset));
  Register #(.width(32)) register_22 (.D(I13), .en(we), .Q(O13), .clk(clk), .clr(reset));
  Register #(.width(32)) register_23 (.D(I21), .en(we), .Q(O21), .clk(clk), .clr(reset));
  Register #(.width(32)) register_24 (.D(I29), .en(we), .Q(O29), .clk(clk), .clr(reset));
  Register #(.width(32)) register_25 (.D(I6), .en(we), .Q(O6), .clk(clk), .clr(reset));
  Register #(.width(32)) register_26 (.D(I14), .en(we), .Q(O14), .clk(clk), .clr(reset));
  Register #(.width(32)) register_27 (.D(I22), .en(we), .Q(O22), .clk(clk), .clr(reset));
  Register #(.width(32)) register_28 (.D(I30), .en(we), .Q(O30), .clk(clk), .clr(reset));
  Register #(.width(32)) register_29 (.D(I7), .en(we), .Q(O7), .clk(clk), .clr(reset));
  Register #(.width(32)) register_30 (.D(I15), .en(we), .Q(O15), .clk(clk), .clr(reset));
  Register #(.width(32)) register_31 (.D(I23), .en(we), .Q(O23), .clk(clk), .clr(reset));
  Register #(.width(32)) register_32 (.D(I31), .en(we), .Q(O31), .clk(clk), .clr(reset));
endmodule

module Decoder (
  input  [5:0] OP,
  input  [5:0] func,
  output out_3,
  output out_4,
  output out_5,
  output out_6,
  output out_7,
  output out_8,
  output out_9,
  output out_10,
  output out_11,
  output out_12,
  output out_13,
  output out_14
);

  and R (out_3, ~OP[5], ~OP[4], ~OP[3], ~OP[2], ~OP[1], ~OP[0]);  // AND_Gate
  and ori (out_5, ~OP[5], ~OP[4], OP[3], OP[2], ~OP[1], OP[0]);  // AND_Gate
  and lw (out_7, OP[5], ~OP[4], ~OP[3], ~OP[2], OP[1], OP[0]);  // AND_Gate
  and sw (out_8, OP[5], ~OP[4], OP[3], ~OP[2], OP[1], OP[0]);  // AND_Gate
  and beq (out_9, ~OP[5], ~OP[4], ~OP[3], OP[2], ~OP[1], ~OP[0]);  // AND_Gate
  and lui (out_11, ~OP[5], ~OP[4], OP[3], OP[2], OP[1], OP[0]);  // AND_Gate
  // AND_Gate slti has open pins: in0=OP[5], in1=OP[4], in2=OP[3], in3=OP[2], in4=OP[1], in5=OP[0], out=open
  // AND_Gate addi has open pins: in0=OP[5], in1=OP[4], in2=OP[3], in3=OP[2], in4=OP[1], in5=OP[0], out=open
  and j (out_13, ~OP[5], ~OP[4], ~OP[3], ~OP[2], OP[1], ~OP[0]);  // AND_Gate
  and jal (out_14, ~OP[5], ~OP[4], ~OP[3], ~OP[2], OP[1], OP[0]);  // AND_Gate
  // AND_Gate bgez has open pins: in0=OP[5], in1=OP[4], in2=OP[3], in3=OP[2], in4=OP[1], in5=OP[0], out=open
  // AND_Gate bgtz has open pins: in0=OP[5], in1=OP[4], in2=OP[3], in3=OP[2], in4=OP[1], in5=OP[0], out=open
  // AND_Gate blez has open pins: in0=OP[5], in1=OP[4], in2=OP[3], in3=OP[2], in4=OP[1], in5=OP[0], out=open
  // AND_Gate bltz has open pins: in0=OP[5], in1=OP[4], in2=OP[3], in3=OP[2], in4=OP[1], in5=OP[0], out=open
  // AND_Gate bne has open pins: in0=OP[5], in1=OP[4], in2=OP[3], in3=OP[2], in4=OP[1], in5=OP[0], out=open
  and addu (out_4, out_3, func[5], ~func[4], ~func[3], ~func[2], ~func[1], func[0]);  // AND_Gate
  and subu (out_6, out_3, func[5], ~func[4], ~func[3], ~func[2], func[1], func[0]);  // AND_Gate
  // AND_Gate and has open pins: in0=out_3, in1=func[5], in2=func[4], in3=func[3], in4=func[2], in5=func[1], in6=func[0], out=open
  // AND_Gate or has open pins: in0=out_3, in1=func[5], in2=func[4], in3=func[3], in4=func[2], in5=func[1], in6=func[0], out=open
  and jr (out_10, out_3, ~func[5], ~func[4], ~func[3], func[2], ~func[1], ~func[0]);  // AND_Gate
  and sll (out_12, out_3, ~func[5], ~func[4], ~func[3], ~func[2], ~func[1], ~func[0]);  // AND_Gate
  // AND_Gate sllv has open pins: in0=out_3, in1=func[5], in2=func[4], in3=func[3], in4=func[2], in5=func[1], in6=func[0], out=open
endmodule

module Controller (
  input  [31:0] Instr,
  output RW,
  output B_beq,
  output B_j,
  output B_jr,
  output [1:0] RegAddr,
  output ALUSrc,
  output [3:0] ALUControl,
  output MemWrite,
  output [1:0] MemtoReg,
  output [1:0] EXTOp,
  output [1:0] DMOp
);

  wire addi, addu, j, jal, lb, lh, lui, lw, ori, Rtype, sb, sh, sll, slti, subu, sw, xor_1_out;

  Decoder decoder_1 (
    .OP(Instr[31:26]), .func(Instr[5:0]), .out_4(addu), .out_5(ori), .out_6(subu), .out_7(lw), .out_8(sw),
    .out_9(B_beq), .out_11(lui), .out_12(sll), .out_13(j), .out_14(jal), .out_10(B_jr), .out_3(Rtype));
  xor xor_1 (xor_1_out, Rtype, B_jr);
  or or_1 (B_j, j, jal);
  buf or_2 (RegAddr[0], Rtype);  // OR_Gate
  buf or_3 (RegAddr[1], jal);  // OR_Gate
  or or_4 (ALUSrc, lw, sw, ori, lui);
  or or_5 (ALUControl[0], subu, sll);
  or or_6 (ALUControl[1], ori, sll);
  buf or_7 (MemtoReg[0], lw);  // OR_Gate
  buf or_8 (MemtoReg[1], jal);  // OR_Gate
  or or_9 (RW, xor_1_out, lw, ori, lui, jal);
  buf sll_sllv (ALUControl[3], sll);  // OR_Gate
  buf or_10 (MemWrite, sw);  // OR_Gate
  // OR_Gate or_11: pin names not known; wires that end beside it: lb, sb, sh, lh, slti, addi, lw, sw, EXTOp[0]
  buf or_12 (EXTOp[1], lui);  // OR_Gate
  buf or_13 (DMOp[0], 1'b0);  // OR_Gate
  buf or_14 (DMOp[1], 1'b0);  // OR_Gate

  assign ALUControl[2] = 1'b0;

  // Other names for the same wires on the sheet: beq = B_beq; jr = B_jr
endmodule

module EXT (
  input  [1:0] in_1,
  input  [15:0] in_2,
  output [31:0] out_3
);

  wire [31:0] bit_extender_1_out, bit_extender_2_out;

  assign bit_extender_1_out = {{16{1'b0}}, in_2};  // Bit_Extender bit_extender_1
  assign bit_extender_2_out = {{16{in_2[15]}}, in_2};  // Bit_Extender bit_extender_2
  Multiplexer #(.select(2), .width(32), .enable("false")) multiplexer_1 (
    .in0(bit_extender_1_out), .in1(bit_extender_2_out), .in2({in_2, {16{1'b0}}}), .out(out_3), .sel(in_1));  // open: in3
endmodule

module ID_EX (
  input  in_1,
  input  in_2,
  input  regwrite,
  input  [1:0] regaddr,
  input  alusrc,
  input  [3:0] aluctrl,
  input  memwrite,
  input  [1:0] memtoreg,
  input  [1:0] DMop,
  input  [31:0] RD1_i,
  input  [31:0] RD2_i,
  input  [4:0] rs_i,
  input  [4:0] rt_i,
  input  [4:0] rd_i,
  input  [31:0] pc_i,
  input  [31:0] pc_4_i,
  input  [31:0] pc_8_i,
  input  [31:0] EXTresult,
  input  in_19,
  input  [31:0] instr_i,
  output out_21,
  output [1:0] out_22,
  output out_23,
  output [3:0] out_24,
  output out_25,
  output [1:0] out_26,
  output [1:0] out_27,
  output [31:0] RD1_o,
  output [31:0] RD2_o,
  output [4:0] rs_o,
  output [4:0] rt_o,
  output [4:0] rd_o,
  output [31:0] pc_o,
  output [31:0] pc_4_o,
  output [31:0] pc_8_o,
  output [31:0] out_36,
  output [31:0] out_37
);

  wire multiplexer_2_out, multiplexer_4_out, multiplexer_6_out;
  wire [1:0] multiplexer_1_out, multiplexer_3_out, multiplexer_7_out;
  wire [3:0] multiplexer_5_out;
  wire [4:0] multiplexer_10_out, multiplexer_11_out, multiplexer_12_out;
  wire [31:0] multiplexer_8_out, multiplexer_9_out, multiplexer_13_out, multiplexer_14_out,
       multiplexer_15_out, multiplexer_16_out, multiplexer_17_out;

  Multiplexer #(.width(2), .enable("false")) multiplexer_1 (
    .in0(DMop), .in1(2'b00), .out(multiplexer_1_out), .sel(in_19));
  Multiplexer #(.enable("false")) multiplexer_2 (.in0(regwrite), .in1(1'b0), .out(multiplexer_2_out), .sel(in_19));
  Multiplexer #(.width(2), .enable("false")) multiplexer_3 (
    .in0(regaddr), .in1(2'b00), .out(multiplexer_3_out), .sel(in_19));
  Multiplexer #(.enable("false")) multiplexer_4 (.in0(alusrc), .in1(1'b0), .out(multiplexer_4_out), .sel(in_19));
  Multiplexer #(.width(4), .enable("false")) multiplexer_5 (
    .in0(aluctrl), .in1(4'b0000), .out(multiplexer_5_out), .sel(in_19));
  Multiplexer #(.enable("false")) multiplexer_6 (.in0(memwrite), .in1(1'b0), .out(multiplexer_6_out), .sel(in_19));
  Multiplexer #(.width(2), .enable("false")) multiplexer_7 (
    .in0(memtoreg), .in1(2'b00), .out(multiplexer_7_out), .sel(in_19));
  Register #(.width(2)) register_1 (.D(multiplexer_1_out), .Q(out_27), .clk(in_1), .clr(in_2));  // open: en
  Multiplexer #(.width(32), .enable("false")) multiplexer_8 (
    .in0(RD1_i), .in1({32{1'b0}}), .out(multiplexer_8_out), .sel(in_19));
  Multiplexer #(.width(32), .enable("false")) multiplexer_9 (
    .in0(RD2_i), .in1({32{1'b0}}), .out(multiplexer_9_out), .sel(in_19));
  Multiplexer #(.width(5), .enable("false")) multiplexer_10 (
    .in0(rs_i), .in1({5{1'b0}}), .out(multiplexer_10_out), .sel(in_19));
  Multiplexer #(.width(5), .enable("false")) multiplexer_11 (
    .in0(rt_i), .in1({5{1'b0}}), .out(multiplexer_11_out), .sel(in_19));
  Multiplexer #(.width(5), .enable("false")) multiplexer_12 (
    .in0(rd_i), .in1({5{1'b0}}), .out(multiplexer_12_out), .sel(in_19));
  Multiplexer #(.width(32), .enable("false")) multiplexer_13 (
    .in0(pc_i), .in1({32{1'b0}}), .out(multiplexer_13_out), .sel(in_19));
  Multiplexer #(.width(32), .enable("false")) multiplexer_14 (
    .in0(pc_4_i), .in1({32{1'b0}}), .out(multiplexer_14_out), .sel(in_19));
  Multiplexer #(.width(32), .enable("false")) multiplexer_15 (
    .in0(pc_8_i), .in1({32{1'b0}}), .out(multiplexer_15_out), .sel(in_19));
  Multiplexer #(.width(32), .enable("false")) multiplexer_16 (
    .in0(EXTresult), .in1({32{1'b0}}), .out(multiplexer_16_out), .sel(in_19));
  Multiplexer #(.width(32), .enable("false")) multiplexer_17 (
    .in0(instr_i), .in1({32{1'b0}}), .out(multiplexer_17_out), .sel(in_19));
  Register #(.width(1)) register_2 (.D(multiplexer_2_out), .Q(out_21), .clk(in_1), .clr(in_2));  // open: en
  Register #(.width(2)) register_3 (.D(multiplexer_3_out), .Q(out_22), .clk(in_1), .clr(in_2));  // open: en
  Register #(.width(1)) register_4 (.D(multiplexer_4_out), .Q(out_23), .clk(in_1), .clr(in_2));  // open: en
  Register #(.width(4)) register_5 (.D(multiplexer_5_out), .Q(out_24), .clk(in_1), .clr(in_2));  // open: en
  Register #(.width(1)) register_6 (.D(multiplexer_6_out), .Q(out_25), .clk(in_1), .clr(in_2));  // open: en
  Register #(.width(2)) register_7 (.D(multiplexer_7_out), .Q(out_26), .clk(in_1), .clr(in_2));  // open: en
  Register #(.width(32)) register_8 (.D(multiplexer_8_out), .Q(RD1_o), .clk(in_1), .clr(in_2));  // open: en
  Register #(.width(32)) register_9 (.D(multiplexer_9_out), .Q(RD2_o), .clk(in_1), .clr(in_2));  // open: en
  Register #(.width(5)) register_10 (.D(multiplexer_10_out), .Q(rs_o), .clk(in_1), .clr(in_2));  // open: en
  Register #(.width(5)) register_11 (.D(multiplexer_11_out), .Q(rt_o), .clk(in_1), .clr(in_2));  // open: en
  Register #(.width(5)) register_12 (.D(multiplexer_12_out), .Q(rd_o), .clk(in_1), .clr(in_2));  // open: en
  Register #(.width(32)) register_13 (.D(multiplexer_13_out), .Q(pc_o), .clk(in_1), .clr(in_2));  // open: en
  Register #(.width(32)) register_14 (.D(multiplexer_14_out), .Q(pc_4_o), .clk(in_1), .clr(in_2));  // open: en
  Register #(.width(32)) register_15 (.D(multiplexer_16_out), .Q(out_36), .clk(in_1), .clr(in_2));  // open: en
  Register #(.width(32)) register_16 (.D(multiplexer_17_out), .Q(out_37), .clk(in_1), .clr(in_2));  // open: en
  Register #(.width(32)) register_17 (.D(multiplexer_15_out), .Q(pc_8_o), .clk(in_1), .clr(in_2));  // open: en

  // Other names for the same wires on the sheet: clk = in_1; clk_prime = in_1; flush = in_19; Reset = in_2
endmodule

module ALU (
  input  [3:0] ALUControl,
  input  [31:0] RD1,
  input  [31:0] RD2,
  input  [4:0] shamt,
  output [31:0] ALUresult
);

  wire [4:0] multiplexer_1_out;
  wire [31:0] adder_1_out, or_out, shifter_1_out, subtractor_1_out;

  Multiplexer #(.width(5), .enable("false")) multiplexer_1 (
    .in0(RD2[4:0]), .in1(shamt), .out(multiplexer_1_out), .sel(ALUControl[3]));
  Adder #(.width(32)) adder_1 (.a(RD1), .b(RD2), .out(adder_1_out));  // open: cin, cout
  Subtractor #(.width(32)) subtractor_1 (.a(RD1), .b(RD2), .out(subtractor_1_out));  // open: bin, bout
  assign or_out = RD1 | RD2;  // OR_Gate or, 32 bits wide
  Shifter #(.width(32)) shifter_1 (.in(RD1), .\dist (multiplexer_1_out), .out(shifter_1_out));
  Multiplexer #(.select(3), .width(32), .enable("false")) multiplexer_2 (
    .in0(adder_1_out), .in1(subtractor_1_out), .in2(or_out), .in3(shifter_1_out), .out(ALUresult),
    .sel(ALUControl[2:0]));  // open: in4, in5, in6, in7

  // Other names for the same wires on the sheet: shamt_t = ALUControl[3]
endmodule

module NPC (
  input  beq,
  input  j_jal,
  input  jr,
  input  zero,
  input  [31:0] pc,
  input  [31:0] instr,
  input  [31:0] extresult,
  input  [31:0] RD1,
  output [31:0] npc
);

  wire and_1_out;
  wire [1:0] or_1_out;
  wire [31:0] adder_1_out, adder_2_out, shifter_1_out;

  Adder #(.width(32)) adder_1 (.a(pc), .b(32'h4), .out(adder_1_out));  // open: cin, cout
  Shifter #(.width(32)) shifter_1 (.in(extresult), .\dist (5'b00010), .out(shifter_1_out));
  Adder #(.width(32)) adder_2 (.a(pc), .b(shifter_1_out), .out(adder_2_out));  // open: cin, cout
  and and_1 (and_1_out, zero, beq);
  Multiplexer #(.select(2), .width(32), .enable("false")) multiplexer_1 (
    .in0(adder_1_out), .in1({pc[31:28], instr[25:0], 2'b00}), .in2(adder_2_out), .in3(RD1), .out(npc),
    .sel(or_1_out));
  or or_1 (or_1_out[0], j_jal, jr);
  or or_2 (or_1_out[1], and_1_out, jr);
endmodule

module npcop (
  input  beq,
  input  jal,
  input  jr,
  output [2:0] NPCop
);

  wire and_1_out, and_2_out, and_3_out, and_4_out, not_1_out, not_2_out, not_3_out, not_4_out, not_5_out,
       not_6_out, not_7_out, not_8_out;

  not not_1 (not_1_out, beq);
  not not_2 (not_2_out, jal);
  not not_3 (not_3_out, beq);
  not not_4 (not_4_out, jr);
  not not_5 (not_5_out, beq);
  not not_6 (not_6_out, jal);
  not not_7 (not_7_out, jal);
  not not_8 (not_8_out, jr);
  and and_1 (and_1_out, not_1_out, not_2_out, jr);
  and and_2 (and_2_out, not_3_out, jal, not_4_out);
  and and_3 (and_3_out, not_5_out, not_6_out, jr);
  and and_4 (and_4_out, beq, not_7_out, not_8_out);
  or or_1 (NPCop[1], and_1_out, and_2_out);
  or or_2 (NPCop[0], and_3_out, and_4_out);

  assign NPCop[2] = 1'b0;
endmodule

module EX_MEM (
  input  in_1,
  input  in_2,
  input  regwrite,
  input  memwrite,
  input  [1:0] memtoreg,
  input  [1:0] DMop,
  input  [31:0] aluresult_i,
  input  [31:0] writedata_i,
  input  [4:0] writereg_i,
  input  [31:0] pc_i,
  input  [31:0] pc_4_i,
  input  [31:0] pc_8_i,
  input  [31:0] instr_i,
  input  [3:0] tnew_E,
  output out_15,
  output out_16,
  output [1:0] out_17,
  output [1:0] out_18,
  output [31:0] out_19,
  output [31:0] out_20,
  output [4:0] out_21,
  output [31:0] pc_o,
  output [31:0] pc_4_o,
  output [31:0] pc_8_o,
  output [31:0] out_25,
  output [3:0] tnew_M
);

  wire comparator_1_lt;
  wire [3:0] multiplexer_1_out, subtractor_1_out;

  Register #(.width(1)) register_1 (.D(regwrite), .Q(out_15), .clk(in_1), .clr(in_2));  // open: en
  Subtractor #(.width(4)) subtractor_1 (.a(tnew_E), .b(4'b0001), .out(subtractor_1_out));  // open: bin, bout
  Comparator #(.width(4)) comparator_1 (.a(subtractor_1_out), .b(4'b0000), .lt(comparator_1_lt));  // open: gt, eq
  Register #(.width(1)) register_2 (.D(memwrite), .Q(out_16), .clk(in_1), .clr(in_2));  // open: en
  Register #(.width(2)) register_3 (.D(memtoreg), .Q(out_17), .clk(in_1), .clr(in_2));  // open: en
  Register #(.width(2)) register_4 (.D(DMop), .Q(out_18), .clk(in_1), .clr(in_2));  // open: en
  Register #(.width(32)) register_5 (.D(aluresult_i), .Q(out_19), .clk(in_1), .clr(in_2));  // open: en
  Register #(.width(32)) register_6 (.D(writedata_i), .Q(out_20), .clk(in_1), .clr(in_2));  // open: en
  Register #(.width(5)) register_7 (.D(writereg_i), .Q(out_21), .clk(in_1), .clr(in_2));  // open: en
  Register #(.width(32)) register_8 (.D(pc_i), .Q(pc_o), .clk(in_1), .clr(in_2));  // open: en
  Register #(.width(32)) register_9 (.D(pc_4_i), .Q(pc_4_o), .clk(in_1), .clr(in_2));  // open: en
  Register #(.width(32)) register_10 (.D(pc_8_i), .Q(pc_8_o), .clk(in_1), .clr(in_2));  // open: en
  Register #(.width(32)) register_11 (.D(instr_i), .Q(out_25), .clk(in_1), .clr(in_2));  // open: en
  Multiplexer #(.width(4), .enable("false")) multiplexer_1 (
    .in0(subtractor_1_out), .in1(4'b0000), .out(multiplexer_1_out), .sel(comparator_1_lt));
  Register #(.width(4)) register_12 (.D(multiplexer_1_out), .Q(tnew_M), .clk(in_1), .clr(in_2));  // open: en

  // Other names for the same wires on the sheet: clk = in_1; clk_prime = in_1; Reset = in_2
endmodule

module DM (
  input  in_1,
  input  in_2,
  input  in_3,
  input  [1:0] DMOp,
  input  [31:0] ALUresult,
  input  [31:0] MemWriteData,
  output [31:0] MemOutData
);

  wire decoder_1_out0, decoder_1_out1, decoder_1_out2, decoder_1_out3, decoder_2_out0, decoder_2_out1;
  wire [1:0] ByteAddr;
  wire [7:0] _0_7, _16_23, _23_31, multiplexer_8_out;
  wire [15:0] multiplexer_9_out;
  wire [15:8] _0_15, _16_31;
  wire [23:0] Addr;
  wire [31:0] LoadByte, LoadHalf, multiplexer_7_out, StoreByte, StoreHalf;

  Bit_Extender #(.in_width(32), .out_width(26)) bit_extender_1 (.in(ALUresult), .out({Addr, ByteAddr}));
  Decoder_part #(.select(2), .enable("false")) decoder_1 (
    .out0(decoder_1_out0), .out1(decoder_1_out1), .out2(decoder_1_out2), .out3(decoder_1_out3), .sel(ByteAddr));
  Decoder_part #(.enable("false")) decoder_2 (.out0(decoder_2_out0), .out1(decoder_2_out1), .sel(ByteAddr[1]));
  Multiplexer #(.width(8), .enable("false")) multiplexer_1 (
    .in0(_0_7), .in1(MemWriteData[7:0]), .out(StoreByte[7:0]), .sel(decoder_1_out0));
  Multiplexer #(.width(8), .enable("false")) multiplexer_2 (
    .in0(_0_15), .in1(MemWriteData[7:0]), .out(StoreByte[15:8]), .sel(decoder_1_out1));
  Multiplexer #(.width(8), .enable("false")) multiplexer_3 (
    .in0(_16_23), .in1(MemWriteData[7:0]), .out(StoreByte[23:16]), .sel(decoder_1_out2));
  Multiplexer #(.width(8), .enable("false")) multiplexer_4 (
    .in0(_23_31), .in1(MemWriteData[7:0]), .out(StoreByte[31:24]), .sel(decoder_1_out3));
  Multiplexer #(.width(16), .enable("false")) multiplexer_5 (
    .in0({_0_15, _0_7}), .in1(MemWriteData[15:0]), .out(StoreHalf[15:0]), .sel(decoder_2_out0));
  Multiplexer #(.width(16), .enable("false")) multiplexer_6 (
    .in0({_16_31, _16_23}), .in1(MemWriteData[15:0]), .out(StoreHalf[31:16]), .sel(decoder_2_out1));
  Multiplexer #(.select(2), .width(32), .enable("false")) multiplexer_7 (
    .in0(MemWriteData), .in1(StoreHalf), .in2(StoreByte), .out(multiplexer_7_out), .sel(DMOp));  // open: in3
  Multiplexer #(.select(2), .width(8), .enable("false")) multiplexer_8 (
    .in0(_0_7), .in1(_0_15), .in2(_16_23), .in3(_16_31), .out(multiplexer_8_out), .sel(ByteAddr));
  Multiplexer #(.width(16), .enable("false")) multiplexer_9 (
    .in0({_0_15, _0_7}), .in1({_16_31, _16_23}), .out(multiplexer_9_out), .sel(ByteAddr[1]));
  RAM #(.addrWidth(24), .dataWidth(32), .bus("separate")) ram_1 (
    .addr(Addr), .din(multiplexer_7_out), .data({_16_31, _16_23, _0_15, _0_7}), .str(in_3), .clk(in_1),
    .clr(in_2));  // open: sel, ld
  assign LoadByte = {{24{multiplexer_8_out[7]}}, multiplexer_8_out};  // Bit_Extender bit_extender_2
  assign LoadHalf = {{16{multiplexer_9_out[15]}}, multiplexer_9_out};  // Bit_Extender bit_extender_3
  Multiplexer #(.select(2), .width(32), .enable("false")) multiplexer_10 (
    .in0({_16_31, _16_23, _0_15, _0_7}), .in1(LoadHalf), .in2(LoadByte), .out(MemOutData), .sel(DMOp));  // open: in3

  // Other names for the same wires on the sheet: HalfAddr = ByteAddr[1]; clk = in_1; _0_15[7:0] = _0_7;
  //   LoadWord[31:0] = {_16_31, _16_23, _0_15, _0_7}; _8_15[7:0] = _0_15; _16_31[7:0] = _16_23; _24_31[7:0] = _16_31;
  //   reset = in_2; Byte[7:0] = MemWriteData[7:0]; Halfword[15:0] = MemWriteData[15:0];
  //   StoreWord[31:0] = MemWriteData; WE = in_3
endmodule

module MEM_WB (
  input  in_1,
  input  in_2,
  input  regwrite,
  input  [1:0] memtoreg,
  input  [4:0] writereg_i,
  input  [31:0] aluresult_i,
  input  [31:0] writedata_i,
  input  [31:0] readdata_i,
  input  [31:0] pc_i,
  input  [31:0] pc_4_i,
  input  [31:0] pc_8_i,
  input  [31:0] instr_i,
  input  [31:0] memaddr,
  input  [31:0] memdata,
  input  memwrite,
  input  [3:0] tnew_M,
  output out_17,
  output [1:0] out_18,
  output [4:0] out_19,
  output [31:0] out_20,
  output [31:0] out_21,
  output [31:0] out_22,
  output [31:0] pc_o,
  output [31:0] pc_4_o,
  output [31:0] pc_8_o,
  output [31:0] out_26,
  output [31:0] out_27,
  output [31:0] out_28,
  output out_29,
  output [3:0] tnew_W
);

  wire comparator_1_lt;
  wire [3:0] multiplexer_1_out, subtractor_1_out;

  Subtractor #(.width(4)) subtractor_1 (.a(tnew_M), .b(4'b0001), .out(subtractor_1_out));  // open: bin, bout
  Register #(.width(1)) register_1 (.D(regwrite), .Q(out_17), .clk(in_1), .clr(in_2));  // open: en
  Register #(.width(2)) register_2 (.D(memtoreg), .Q(out_18), .clk(in_1), .clr(in_2));  // open: en
  Register #(.width(5)) register_3 (.D(writereg_i), .Q(out_19), .clk(in_1), .clr(in_2));  // open: en
  Comparator #(.width(4)) comparator_1 (.a(subtractor_1_out), .b(4'b0000), .lt(comparator_1_lt));  // open: gt, eq
  Register #(.width(32)) register_4 (.D(aluresult_i), .Q(out_20), .clk(in_1), .clr(in_2));  // open: en
  Register #(.width(32)) register_5 (.D(writedata_i), .Q(out_21), .clk(in_1), .clr(in_2));  // open: en
  Register #(.width(32)) register_6 (.D(readdata_i), .Q(out_22), .clk(in_1), .clr(in_2));  // open: en
  Register #(.width(32)) register_7 (.D(pc_i), .Q(pc_o), .clk(in_1), .clr(in_2));  // open: en
  Register #(.width(32)) register_8 (.D(pc_4_i), .Q(pc_4_o), .clk(in_1), .clr(in_2));  // open: en
  Register #(.width(32)) register_9 (.D(pc_8_i), .Q(pc_8_o), .clk(in_1), .clr(in_2));  // open: en
  Register #(.width(32)) register_10 (.D(instr_i), .Q(out_26), .clk(in_1), .clr(in_2));  // open: en
  Register #(.width(32)) register_11 (.D(memaddr), .Q(out_27), .clk(in_1), .clr(in_2));  // open: en
  Register #(.width(32)) register_12 (.D(memdata), .Q(out_28), .clk(in_1), .clr(in_2));  // open: en
  Register #(.width(1)) register_13 (.D(memwrite), .Q(out_29), .clk(in_1), .clr(in_2));  // open: en
  Multiplexer #(.width(4), .enable("false")) multiplexer_1 (
    .in0(subtractor_1_out), .in1(4'b0000), .out(multiplexer_1_out), .sel(comparator_1_lt));
  Register #(.width(4)) register_14 (.D(multiplexer_1_out), .Q(tnew_W), .clk(in_1), .clr(in_2));  // open: en

  // Other names for the same wires on the sheet: clk = in_1; clk_prime = in_1; Reset = in_2
endmodule

module D (
  input  [31:0] Instr,
  output [4:0] S1_D,
  output [4:0] S2_D,
  output [1:0] tuse1_D,
  output [1:0] tuse2_D
);

  wire decoder_1_out_4, decoder_1_out_5, decoder_1_out_6, decoder_1_out_7, decoder_1_out_8, decoder_1_out_9,
       decoder_1_out_10, decoder_1_out_11, decoder_1_out_12, decoder_1_out_13, decoder_1_out_14, or_1_out,
       or_2_out, or_3_out, or_4_out;
  wire [1:0] bit_extender_1_out;
  wire [4:0] splitter_1__16_20, splitter_1__21_25;

  Decoder decoder_1 (
    .OP(Instr[31:26]), .func(Instr[5:0]), .out_4(decoder_1_out_4), .out_5(decoder_1_out_5),
    .out_6(decoder_1_out_6), .out_7(decoder_1_out_7), .out_8(decoder_1_out_8), .out_9(decoder_1_out_9),
    .out_11(decoder_1_out_11), .out_12(decoder_1_out_12), .out_13(decoder_1_out_13),
    .out_14(decoder_1_out_14), .out_10(decoder_1_out_10));  // open: out_3
  Splitter splitter_1 (
    .INPUT(Instr), ._21_25(splitter_1__21_25), ._16_20(splitter_1__16_20));  // open: _11_15, _0_15, _0_25
  or or_1 (or_1_out, decoder_1_out_4, decoder_1_out_6, decoder_1_out_5, decoder_1_out_7, decoder_1_out_8, decoder_1_out_9, decoder_1_out_12);
  Multiplexer #(.width(5), .enable("false")) multiplexer_1 (
    .in0({5{1'b0}}), .in1(splitter_1__21_25), .out(S1_D), .sel(or_1_out));
  or or_2 (or_2_out, decoder_1_out_4, decoder_1_out_6, decoder_1_out_8, decoder_1_out_9);
  Multiplexer #(.width(5), .enable("false")) multiplexer_2 (
    .in0({5{1'b0}}), .in1(splitter_1__16_20), .out(S2_D), .sel(or_2_out));
  or or_3 (or_3_out, decoder_1_out_4, decoder_1_out_6, decoder_1_out_7, decoder_1_out_8, decoder_1_out_5);
  Multiplexer #(.width(2), .enable("false")) multiplexer_3 (.in0(2'b00), .in1(2'b01), .out(tuse1_D), .sel(or_3_out));
  or or_4 (or_4_out, decoder_1_out_4, decoder_1_out_6, decoder_1_out_12);
  assign bit_extender_1_out = {{1{1'b0}}, or_4_out};  // Bit_Extender bit_extender_1
  Multiplexer #(.width(2), .enable("false")) multiplexer_4 (
    .in0(bit_extender_1_out), .in1(2'b10), .out(tuse2_D), .sel(decoder_1_out_7));
endmodule

module E (
  input  [31:0] Instr,
  input  [31:0] extendresult,
  input  [31:0] pc_8,
  output [4:0] S1_E,
  output [4:0] S2_E,
  output [3:0] tnew_E,
  output [4:0] Des_E,
  output [31:0] etod
);

  wire decoder_1_out_4, decoder_1_out_5, decoder_1_out_6, decoder_1_out_7, decoder_1_out_8, decoder_1_out_9,
       decoder_1_out_10, decoder_1_out_11, decoder_1_out_12, decoder_1_out_13, decoder_1_out_14, or_1_out,
       or_2_out;
  wire [1:0] or_6_out;
  wire [4:0] splitter_1__11_15, splitter_1__16_20, splitter_1__21_25;

  Decoder decoder_1 (
    .OP(Instr[31:26]), .func(Instr[5:0]), .out_4(decoder_1_out_4), .out_5(decoder_1_out_5),
    .out_6(decoder_1_out_6), .out_7(decoder_1_out_7), .out_8(decoder_1_out_8), .out_9(decoder_1_out_9),
    .out_11(decoder_1_out_11), .out_12(decoder_1_out_12), .out_13(decoder_1_out_13),
    .out_14(decoder_1_out_14), .out_10(decoder_1_out_10));  // open: out_3
  Splitter splitter_1 (
    .INPUT(Instr), ._21_25(splitter_1__21_25), ._16_20(splitter_1__16_20), ._11_15(splitter_1__11_15));  // open: _0_15, _0_25
  or or_1 (or_1_out, decoder_1_out_4, decoder_1_out_6, decoder_1_out_5, decoder_1_out_7, decoder_1_out_8, decoder_1_out_12);
  Multiplexer #(.width(5), .enable("false")) multiplexer_1 (
    .in0({5{1'b0}}), .in1(splitter_1__21_25), .out(S1_E), .sel(or_1_out));
  or or_2 (or_2_out, decoder_1_out_4, decoder_1_out_6, decoder_1_out_8);
  Multiplexer #(.width(5), .enable("false")) multiplexer_2 (
    .in0({5{1'b0}}), .in1(splitter_1__16_20), .out(S2_E), .sel(or_2_out));
  buf or_3 (tnew_E[1], decoder_1_out_7);  // OR_Gate
  Multiplexer #(.width(32), .enable("false")) multiplexer_3 (
    .in0(extendresult), .in1(pc_8), .out(etod), .sel(decoder_1_out_14));
  or or_4 (tnew_E[0], decoder_1_out_4, decoder_1_out_6, decoder_1_out_12, decoder_1_out_11);
  or or_5 (or_6_out[1], decoder_1_out_4, decoder_1_out_6, decoder_1_out_12, decoder_1_out_14);
  or or_6 (or_6_out[0], decoder_1_out_7, decoder_1_out_11, decoder_1_out_5, decoder_1_out_14);
  Multiplexer #(.select(2), .width(5), .enable("false")) multiplexer_4 (
    .in0({5{1'b0}}), .in1(splitter_1__16_20), .in2(splitter_1__11_15), .in3({5{1'b1}}), .out(Des_E),
    .sel(or_6_out));

  assign tnew_E[3:2] = 2'b00;
endmodule

module M (
  input  [31:0] Instr,
  input  [31:0] pc_8,
  input  [31:0] aluresult,
  output [4:0] S1_M,
  output [4:0] S2_M,
  output [4:0] Des_E,
  output [31:0] mtod
);

  wire decoder_1_out_4, decoder_1_out_5, decoder_1_out_6, decoder_1_out_7, decoder_1_out_8, decoder_1_out_9,
       decoder_1_out_10, decoder_1_out_11, decoder_1_out_12, decoder_1_out_13, decoder_1_out_14, or_1_out,
       or_2_out, or_3_out;
  wire [1:0] or_5_out;
  wire [4:0] splitter_1__11_15, splitter_1__16_20, splitter_1__21_25;

  Decoder decoder_1 (
    .OP(Instr[31:26]), .func(Instr[5:0]), .out_4(decoder_1_out_4), .out_5(decoder_1_out_5),
    .out_6(decoder_1_out_6), .out_7(decoder_1_out_7), .out_8(decoder_1_out_8), .out_9(decoder_1_out_9),
    .out_11(decoder_1_out_11), .out_12(decoder_1_out_12), .out_13(decoder_1_out_13),
    .out_14(decoder_1_out_14), .out_10(decoder_1_out_10));  // open: out_3
  Splitter splitter_1 (
    .INPUT(Instr), ._21_25(splitter_1__21_25), ._16_20(splitter_1__16_20), ._11_15(splitter_1__11_15));  // open: _0_15, _0_25
  buf or_1 (or_1_out, 1'b0);  // OR_Gate
  Multiplexer #(.width(5), .enable("false")) multiplexer_1 (
    .in0({5{1'b0}}), .in1(splitter_1__21_25), .out(S1_M), .sel(or_1_out));
  buf or_2 (or_2_out, decoder_1_out_8);  // OR_Gate
  Multiplexer #(.width(5), .enable("false")) multiplexer_2 (
    .in0({5{1'b0}}), .in1(splitter_1__16_20), .out(S2_M), .sel(or_2_out));
  or or_3 (or_3_out, decoder_1_out_4, decoder_1_out_6, decoder_1_out_5, decoder_1_out_11);
  or or_4 (or_5_out[1], decoder_1_out_4, decoder_1_out_6, decoder_1_out_14);
  Multiplexer #(.width(32), .enable("false")) multiplexer_3 (.in0(pc_8), .in1(aluresult), .out(mtod), .sel(or_3_out));
  or or_5 (or_5_out[0], decoder_1_out_7, decoder_1_out_11, decoder_1_out_5, decoder_1_out_14);
  Multiplexer #(.select(2), .width(5), .enable("false")) multiplexer_4 (
    .in0({5{1'b0}}), .in1(splitter_1__16_20), .in2(splitter_1__11_15), .in3({5{1'b1}}), .out(Des_E),
    .sel(or_5_out));
endmodule

module W (
  input  [31:0] Instr,
  input  [31:0] aluresult,
  input  [31:0] pc_8,
  input  [31:0] regdata,
  output [4:0] Des_E,
  output [31:0] wtod
);

  wire decoder_1_out_4, decoder_1_out_5, decoder_1_out_6, decoder_1_out_7, decoder_1_out_8, decoder_1_out_9,
       decoder_1_out_10, decoder_1_out_11, decoder_1_out_12, decoder_1_out_13, decoder_1_out_14;
  wire [1:0] or_2_out, or_4_out;
  wire [4:0] splitter_1__11_15, splitter_1__16_20;

  Decoder decoder_1 (
    .OP(Instr[31:26]), .func(Instr[5:0]), .out_4(decoder_1_out_4), .out_5(decoder_1_out_5),
    .out_6(decoder_1_out_6), .out_7(decoder_1_out_7), .out_8(decoder_1_out_8), .out_9(decoder_1_out_9),
    .out_11(decoder_1_out_11), .out_12(decoder_1_out_12), .out_13(decoder_1_out_13),
    .out_14(decoder_1_out_14), .out_10(decoder_1_out_10));  // open: out_3
  Splitter splitter_1 (
    .INPUT(Instr), ._16_20(splitter_1__16_20), ._11_15(splitter_1__11_15));  // open: _21_25, _0_15, _0_25
  or or_1 (or_2_out[1], decoder_1_out_14, decoder_1_out_7);
  or or_2 (or_2_out[0], decoder_1_out_7, decoder_1_out_4, decoder_1_out_6, decoder_1_out_5, decoder_1_out_11);
  or or_3 (or_4_out[1], decoder_1_out_4, decoder_1_out_6, decoder_1_out_14);
  Multiplexer #(.select(2), .width(32), .enable("false")) multiplexer_1 (
    .in0({32{1'b0}}), .in1(aluresult), .in2(pc_8), .in3(regdata), .out(wtod), .sel(or_2_out));
  or or_4 (or_4_out[0], decoder_1_out_14, decoder_1_out_5, decoder_1_out_11, decoder_1_out_7);
  Multiplexer #(.select(2), .width(5), .enable("false")) multiplexer_2 (
    .in0({5{1'b0}}), .in1(splitter_1__16_20), .in2(splitter_1__11_15), .in3({5{1'b1}}), .out(Des_E),
    .sel(or_4_out));
endmodule
