// Logisim project singleCPU.circ as structural Verilog: 8 circuits, main circuit ALU
module ALU (
  input  [3:0] ALUControl,
  input  [31:0] A,
  input  [31:0] B,
  input  [4:0] shamt,
  output [31:0] C,
  output Zero
);

  wire comparator_1_lt;
  wire [4:0] multiplexer_1_out;
  wire [31:0] adder_1_out, and_1_out, bit_extender_1_out, or_1_out, shifter_1_out, subtractor_1_out;

  Multiplexer #(.width(5), .enable("false")) multiplexer_1 (
    .in0(A[4:0]), .in1(shamt), .out(multiplexer_1_out), .sel(ALUControl[3]));
  Adder #(.width(32)) adder_1 (.a(A), .b(B), .out(adder_1_out));  // open: cin, cout
  Subtractor #(.width(32)) subtractor_1 (.a(A), .b(B), .out(subtractor_1_out));  // open: bin, bout
  assign or_1_out = A | B;  // OR_Gate or_1, 32 bits wide
  assign and_1_out = A & B;  // AND_Gate and_1, 32 bits wide
  Comparator #(.width(32)) comparator_1 (.a(A), .b(B), .eq(Zero), .lt(comparator_1_lt));  // open: gt
  Shifter #(.width(32)) shifter_1 (.in(B), .\dist (multiplexer_1_out), .out(shifter_1_out));
  assign bit_extender_1_out = {{31{1'b0}}, comparator_1_lt};  // Bit_Extender bit_extender_1
  Multiplexer #(.select(3), .width(32), .enable("false")) multiplexer_2 (
    .in0(adder_1_out), .in1(subtractor_1_out), .in2(or_1_out), .in3(and_1_out), .in4(bit_extender_1_out),
    .in5(shifter_1_out), .out(C), .sel(ALUControl[2:0]));  // open: in6, in7

  // Other names for the same wires on the sheet: ShamtSrc = ALUControl[3]

  // Notes on the sheet:
  //   F  000加法 001减法 010或 011与 100SLT 101sll/sllv
endmodule

module GRF (
  input  CLK,
  input  reset,
  input  WE,
  input  [4:0] A1,
  input  [4:0] A2,
  input  [4:0] A3,
  input  [31:0] WD,
  output [31:0] RD1,
  output [31:0] RD2
);

  wire [31:0] O0, O1, O2, O3, O4, O5, O6, O7, O8, O9, O10, O11, O12, O13, O14, O15, O16, O17, O18, O19, O20,
       O21, O22, O23, O24, O25, O26, O27, O28, O29, O30, O31, R1, R2, R3, R4, R5, R6, R7, R8, R9, R10, R11,
       R12, R13, R14, R15, R16, R17, R18, R19, R20, R21, R22, R23, R24, R25, R26, R27, R28, R29, R30, R31;

  Demultiplexer #(.select(5), .width(32), .tristate("true"), .disabled(0)) demultiplexer_1 (
    .out1(R1), .out2(R2), .out3(R3), .out4(R4), .out5(R5), .out6(R6), .out7(R7), .out8(R8), .out9(R9),
    .out10(R10), .out11(R11), .out12(R12), .out13(R13), .out14(R14), .out15(R15), .out16(R16), .out17(R17),
    .out18(R18), .out19(R19), .out20(R20), .out21(R21), .out22(R22), .out23(R23), .out24(R24), .out25(R25),
    .out26(R26), .out27(R27), .out28(R28), .out29(R29), .out30(R30), .out31(R31), .in(WD), .sel(A3));  // open: out0, en
  Register #(.width(32)) register_1 (.D({32{1'b0}}), .en(1'b1), .Q(O0), .clk(CLK), .clr(reset));
  Register #(.width(32)) register_2 (.D(R1), .en(WE), .Q(O1), .clk(CLK), .clr(reset));
  Register #(.width(32)) register_3 (.D(R2), .en(WE), .Q(O2), .clk(CLK), .clr(reset));
  Register #(.width(32)) register_4 (.D(R3), .en(WE), .Q(O3), .clk(CLK), .clr(reset));
  Register #(.width(32)) register_5 (.D(R4), .en(WE), .Q(O4), .clk(CLK), .clr(reset));
  Register #(.width(32)) register_6 (.D(R5), .en(WE), .Q(O5), .clk(CLK), .clr(reset));
  Register #(.width(32)) register_7 (.D(R6), .en(WE), .Q(O6), .clk(CLK), .clr(reset));
  Register #(.width(32)) register_8 (.D(R7), .en(WE), .Q(O7), .clk(CLK), .clr(reset));
  Register #(.width(32)) register_9 (.D(R8), .en(WE), .Q(O8), .clk(CLK), .clr(reset));
  Register #(.width(32)) register_10 (.D(R9), .en(WE), .Q(O9), .clk(CLK), .clr(reset));
  Register #(.width(32)) register_11 (.D(R10), .en(WE), .Q(O10), .clk(CLK), .clr(reset));
  Register #(.width(32)) register_12 (.D(R11), .en(WE), .Q(O11), .clk(CLK), .clr(reset));
  Register #(.width(32)) register_13 (.D(R12), .en(WE), .Q(O12), .clk(CLK), .clr(reset));
  Register #(.width(32)) register_14 (.D(R13), .en(WE), .Q(O13), .clk(CLK), .clr(reset));
  Register #(.width(32)) register_15 (.D(R14), .en(WE), .Q(O14), .clk(CLK), .clr(reset));
  Register #(.width(32)) register_16 (.D(R15), .en(WE), .Q(O15), .clk(CLK), .clr(reset));
  Register #(.width(32)) register_17 (.D(R16), .en(WE), .Q(O16), .clk(CLK), .clr(reset));
  Register #(.width(32)) register_18 (.D(R17), .en(WE), .Q(O17), .clk(CLK), .clr(reset));
  Register #(.width(32)) register_19 (.D(R18), .en(WE), .Q(O18), .clk(CLK), .clr(reset));
  Register #(.width(32)) register_20 (.D(R19), .en(WE), .Q(O19), .clk(CLK), .clr(reset));
  Register #(.width(32)) register_21 (.D(R20), .en(WE), .Q(O20), .clk(CLK), .clr(reset));
  Register #(.width(32)) register_22 (.D(R21), .en(WE), .Q(O21), .clk(CLK), .clr(reset));
  Register #(.width(32)) register_23 (.D(R22), .en(WE), .Q(O22), .clk(CLK), .clr(reset));
  Register #(.width(32)) register_24 (.D(R23), .en(WE), .Q(O23), .clk(CLK), .clr(reset));
  Register #(.width(32)) register_25 (.D(R24), .en(WE), .Q(O24), .clk(CLK), .clr(reset));
  Register #(.width(32)) register_26 (.D(R25), .en(WE), .Q(O25), .clk(CLK), .clr(reset));
  Register #(.width(32)) register_27 (.D(R26), .en(WE), .Q(O26), .clk(CLK), .clr(reset));
  Register #(.width(32)) register_28 (.D(R27), .en(WE), .Q(O27), .clk(CLK), .clr(reset));
  Register #(.width(32)) register_29 (.D(R28), .en(WE), .Q(O28), .clk(CLK), .clr(reset));
  Register #(.width(32)) register_30 (.D(R29), .en(WE), .Q(O29), .clk(CLK), .clr(reset));
  Register #(.width(32)) register_31 (.D(R30), .en(WE), .Q(O30), .clk(CLK), .clr(reset));
  Register #(.width(32)) register_32 (.D(R31), .en(WE), .Q(O31), .clk(CLK), .clr(reset));
  Multiplexer #(.select(5), .width(32), .disabled(0)) multiplexer_1 (
    .in0(O0), .in1(O1), .in2(O2), .in3(O3), .in4(O4), .in5(O5), .in6(O6), .in7(O7), .in8(O8), .in9(O9),
    .in10(O10), .in11(O11), .in12(O12), .in13(O13), .in14(O14), .in15(O15), .in16(O16), .in17(O17),
    .in18(O18), .in19(O19), .in20(O20), .in21(O21), .in22(O22), .in23(O23), .in24(O24), .in25(O25),
    .in26(O26), .in27(O27), .in28(O28), .in29(O29), .in30(O30), .in31(O31), .out(RD1), .sel(A1));  // open: en
  Multiplexer #(.select(5), .width(32), .disabled(0)) multiplexer_2 (
    .in0(O0), .in1(O1), .in2(O2), .in3(O3), .in4(O4), .in5(O5), .in6(O6), .in7(O7), .in8(O8), .in9(O9),
    .in10(O10), .in11(O11), .in12(O12), .in13(O13), .in14(O14), .in15(O15), .in16(O16), .in17(O17),
    .in18(O18), .in19(O19), .in20(O20), .in21(O21), .in22(O22), .in23(O23), .in24(O24), .in25(O25),
    .in26(O26), .in27(O27), .in28(O28), .in29(O29), .in30(O30), .in31(O31), .out(RD2), .sel(A2));  // open: en
endmodule

module IFU (
  input  in_1,
  input  reset,
  input  [31:0] NPC,
  output [31:0] Instr,
  output [31:0] out_5
);

  Register #(.width(32)) register_1 (.D(NPC), .Q(out_5), .clk(in_1), .clr(reset));  // open: en
  ROM #(.addrWidth(5), .dataWidth(32)) rom_1 (.addr(out_5[6:2]), .data(Instr));  // open: sel

  // Other names for the same wires on the sheet: clk = in_1; PCnow[31:0] = out_5

  // Notes on the sheet:
  //   contents of rom_1 (hex, n*v repeats v):
  //   c000c02 295a021 369400bb 3e00008
endmodule

module DM (
  input  in_1,
  input  in_2,
  input  in_3,
  input  [1:0] DMOp,
  input  [6:0] ALUresult,
  input  [31:0] MemWriteData,
  output [31:0] MemOutData
);

  wire decoder_1_out0, decoder_1_out1, decoder_1_out2, decoder_1_out3, decoder_2_out0, decoder_2_out1;
  wire [7:0] _0_7, _16_23, _23_31, multiplexer_8_out;
  wire [15:0] multiplexer_9_out;
  wire [15:8] _0_15, _16_31;
  wire [31:0] LoadByte, LoadHalf, multiplexer_7_out, StoreByte, StoreHalf;

  Decoder #(.select(2), .enable("false")) decoder_1 (
    .out0(decoder_1_out0), .out1(decoder_1_out1), .out2(decoder_1_out2), .out3(decoder_1_out3),
    .sel(ALUresult[1:0]));
  Decoder #(.enable("false")) decoder_2 (.out0(decoder_2_out0), .out1(decoder_2_out1), .sel(ALUresult[1]));
  Multiplexer #(.width(8), .enable("false")) multiplexer_1 (
    .in0(_0_7), .in1(MemWriteData[7:0]), .out(StoreByte[7:0]), .sel(decoder_1_out0));
  Multiplexer #(.width(8), .enable("false")) multiplexer_2 (
    .in0(_0_15), .in1(MemWriteData[7:0]), .out(StoreByte[15:8]), .sel(decoder_1_out1));
  Multiplexer #(.width(8), .enable("false")) multiplexer_3 (
    .in0(_16_23), .in1(MemWriteData[7:0]), .out(StoreByte[23:16]), .sel(decoder_1_out2));
  Multiplexer #(.width(8), .enable("false")) multiplexer_4 (
    .in0(_23_31), .in1(MemWriteData[7:0]), .out(StoreByte[31:24]), .sel(decoder_1_out3));
  Multiplexer #(.width(16), .enable("false")) multiplexer_5 (
    .in0({_0_15, _0_7}), .in1(MemWriteData[15:0]), .out(StoreHalf[15:0]), .sel(decoder_2_out0));
  Multiplexer #(.width(16), .enable("false")) multiplexer_6 (
    .in0({_16_31, _16_23}), .in1(MemWriteData[15:0]), .out(StoreHalf[31:16]), .sel(decoder_2_out1));
  Multiplexer #(.select(2), .width(32), .enable("false")) multiplexer_7 (
    .in0(MemWriteData), .in1(StoreHalf), .in2(StoreByte), .out(multiplexer_7_out), .sel(DMOp));  // open: in3
  Multiplexer #(.select(2), .width(8), .enable("false")) multiplexer_8 (
    .in0(_0_7), .in1(_0_15), .in2(_16_23), .in3(_16_31), .out(multiplexer_8_out), .sel(ALUresult[1:0]));
  Multiplexer #(.width(16), .enable("false")) multiplexer_9 (
    .in0({_0_15, _0_7}), .in1({_16_31, _16_23}), .out(multiplexer_9_out), .sel(ALUresult[1]));
  RAM #(.addrWidth(5), .dataWidth(32), .bus("separate")) ram_1 (
    .addr(ALUresult[6:2]), .din(multiplexer_7_out), .data({_16_31, _16_23, _0_15, _0_7}), .str(in_3),
    .clk(in_1), .clr(in_2));  // open: sel, ld
  assign LoadByte = {{24{multiplexer_8_out[7]}}, multiplexer_8_out};  // Bit_Extender bit_extender_1
  assign LoadHalf = {{16{multiplexer_9_out[15]}}, multiplexer_9_out};  // Bit_Extender bit_extender_2
  Multiplexer #(.select(2), .width(32), .enable("false")) multiplexer_10 (
    .in0({_16_31, _16_23, _0_15, _0_7}), .in1(LoadHalf), .in2(LoadByte), .out(MemOutData), .sel(DMOp));  // open: in3

  // Other names for the same wires on the sheet: ByteAddr[1:0] = ALUresult[1:0]; HalfAddr = ALUresult[1];
  //   Addr[4:0] = ALUresult[6:2]; clk = in_1; _0_15[7:0] = _0_7; LoadWord[31:0] = {_16_31, _16_23, _0_15, _0_7};
  //   _8_15[7:0] = _0_15; _16_31[7:0] = _16_23; _24_31[7:0] = _16_31; reset = in_2; Byte[7:0] = MemWriteData[7:0];
  //   Halfword[15:0] = MemWriteData[15:0]; StoreWord[31:0] = MemWriteData; WE = in_3
endmodule

module Controller (
  input  [5:0] OP,
  input  [5:0] func,
  output RW,
  output [1:0] RegAddr,
  output ALUSrc,
  output [3:0] ALUControl,
  output [3:0] NPCOp,
  output MemWrite,
  output [1:0] MemtoReg,
  output [1:0] EXTOp,
  output [1:0] DMOp
);

  wire addi, addu, \and , beq, bgez, bgtz, bltz, bne, j, jal, jr, lui, lw, \or , ori, Rtype, sll, sllv, slti,
       subu, sw, xor_1_out;

  and R (Rtype, ~OP[5], ~OP[4], ~OP[3], ~OP[2], ~OP[1], ~OP[0]);  // AND_Gate
  and u_ori (ori, ~OP[5], ~OP[4], OP[3], OP[2], ~OP[1], OP[0]);  // AND_Gate
  and u_lw (lw, OP[5], ~OP[4], ~OP[3], ~OP[2], OP[1], OP[0]);  // AND_Gate
  and u_sw (sw, OP[5], ~OP[4], OP[3], ~OP[2], OP[1], OP[0]);  // AND_Gate
  and u_beq (beq, ~OP[5], ~OP[4], ~OP[3], OP[2], ~OP[1], ~OP[0]);  // AND_Gate
  and u_lui (lui, ~OP[5], ~OP[4], OP[3], OP[2], OP[1], OP[0]);  // AND_Gate
  and u_slti (slti, ~OP[5], ~OP[4], OP[3], ~OP[2], OP[1], ~OP[0]);  // AND_Gate
  and u_addi (addi, ~OP[5], ~OP[4], OP[3], ~OP[2], ~OP[1], ~OP[0]);  // AND_Gate
  and u_j (j, ~OP[5], ~OP[4], ~OP[3], ~OP[2], OP[1], ~OP[0]);  // AND_Gate
  and u_jal (jal, ~OP[5], ~OP[4], ~OP[3], ~OP[2], OP[1], OP[0]);  // AND_Gate
  and u_bgez (bgez, ~OP[5], ~OP[4], ~OP[3], ~OP[2], ~OP[1], OP[0]);  // AND_Gate
  and u_bgtz (bgtz, ~OP[5], ~OP[4], ~OP[3], OP[2], OP[1], OP[0]);  // AND_Gate
  // AND_Gate blez has open pins: in0=OP[5], in1=OP[4], in2=OP[3], in3=OP[2], in4=OP[1], in5=OP[0], out=open
  and u_bltz (bltz, ~OP[5], ~OP[4], ~OP[3], ~OP[2], ~OP[1], OP[0]);  // AND_Gate
  and u_bne (bne, ~OP[5], ~OP[4], ~OP[3], OP[2], ~OP[1], OP[0]);  // AND_Gate
  and u_addu (addu, Rtype, func[5], ~func[4], ~func[3], ~func[2], ~func[1], func[0]);  // AND_Gate
  and u_subu (subu, Rtype, func[5], ~func[4], ~func[3], ~func[2], func[1], func[0]);  // AND_Gate
  and u_and (\and , Rtype, func[5], ~func[4], ~func[3], func[2], ~func[1], ~func[0]);  // AND_Gate
  and u_or (\or , Rtype, func[5], ~func[4], ~func[3], func[2], ~func[1], func[0]);  // AND_Gate
  and u_jr (jr, Rtype, ~func[5], ~func[4], ~func[3], func[2], ~func[1], ~func[0]);  // AND_Gate
  and u_sll (sll, Rtype, ~func[5], ~func[4], ~func[3], ~func[2], ~func[1], ~func[0]);  // AND_Gate
  and u_sllv (sllv, Rtype, ~func[5], ~func[4], ~func[3], func[2], ~func[1], ~func[0]);  // AND_Gate
  buf or_2 (RegAddr[0], Rtype);  // OR_Gate
  buf or_3 (RegAddr[1], jal);  // OR_Gate
  or or_4 (ALUControl[0], subu, \and , sll, sllv);
  or or_5 (ALUControl[1], \and , \or , ori);
  or or_6 (ALUControl[2], slti, sll, sllv);
  buf sll_sllv (ALUControl[3], sll);  // OR_Gate
  or or_7 (NPCOp[1], jr, bne, bgtz);
  or or_8 (NPCOp[2], jr, j, jal, bltz);
  buf or_9 (MemWrite, sw);  // OR_Gate
  buf or_10 (MemtoReg[0], lw);  // OR_Gate
  buf or_11 (MemtoReg[1], jal);  // OR_Gate
  or or_12 (ALUSrc, lw, sw, ori, lui, slti, addi);
  or or_13 (NPCOp[0], beq, bgtz, j, jal);
  or or_14 (EXTOp[0], lw, sw, slti, addi);
  buf or_15 (EXTOp[1], lui);  // OR_Gate
  buf or_16 (DMOp[0], 1'b0);  // OR_Gate
  buf or_17 (DMOp[1], 1'b0);  // OR_Gate
  xor xor_1 (xor_1_out, Rtype, jr);
  or or_18 (RW, xor_1_out, lw, ori, lui, slti, addi, jal);

  assign NPCOp[3] = 1'b0;
endmodule

module EXT (
  input  [1:0] in_1,
  input  [15:0] in_2,
  output [31:0] out_3
);

  wire [31:0] bit_extender_1_out, bit_extender_2_out;

  assign bit_extender_1_out = {{16{1'b0}}, in_2};  // Bit_Extender bit_extender_1
  assign bit_extender_2_out = {{16{in_2[15]}}, in_2};  // Bit_Extender bit_extender_2
  Multiplexer #(.select(2), .width(32), .enable("false")) multiplexer_1 (
    .in0(bit_extender_1_out), .in1(bit_extender_2_out), .in2({in_2, {16{1'b0}}}), .out(out_3), .sel(in_1));  // open: in3
endmodule

module NPC (
  input  in_1,
  input  [31:0] PCnow,
  input  [3:0] NPCOp,
  input  [25:0] Imm,
  input  [31:0] RD1,
  output [31:0] PC_4,
  output [31:0] NPC
);

  wire bgez, bgtz, blez, bltz, comparator_1_eq;
  wire [15:0] shifter_1_out;
  wire [31:0] beqAddr, bgezAddr, bgtzAddr, bit_extender_1_out, blezAddr, bltzAddr, bneAddr, BranchAddr;

  Adder #(.width(32)) adder_1 (.a(PCnow), .b(32'h4), .out(PC_4));  // open: cin, cout
  assign bit_extender_1_out = {{16{shifter_1_out[15]}}, shifter_1_out};  // Bit_Extender bit_extender_1
  Shifter #(.width(16)) shifter_1 (.in(Imm[15:0]), .\dist (4'b0010), .out(shifter_1_out));
  Comparator #(.width(32)) comparator_1 (.a(RD1), .b({32{1'b0}}), .gt(bgtz), .eq(comparator_1_eq), .lt(bltz));
  Multiplexer #(.width(32), .enable("false")) multiplexer_1 (.in0(PC_4), .in1(BranchAddr), .out(beqAddr), .sel(in_1));
  Multiplexer #(.width(32), .enable("false")) multiplexer_2 (.in0(BranchAddr), .in1(PC_4), .out(bneAddr), .sel(in_1));
  Multiplexer #(.width(32), .enable("false")) multiplexer_3 (.in0(PC_4), .in1(BranchAddr), .out(bgtzAddr), .sel(bgtz));
  Adder #(.width(32)) adder_2 (.a(PC_4), .b(bit_extender_1_out), .out(BranchAddr));  // open: cin, cout
  or or_1 (bgez, bgtz, comparator_1_eq);
  or or_2 (blez, comparator_1_eq, bltz);
  Multiplexer #(.width(32), .enable("false")) multiplexer_4 (.in0(PC_4), .in1(BranchAddr), .out(bgezAddr), .sel(bgez));
  Multiplexer #(.width(32), .enable("false")) multiplexer_5 (.in0(PC_4), .in1(BranchAddr), .out(bltzAddr), .sel(bltz));
  Multiplexer #(.width(32), .enable("false")) multiplexer_6 (.in0(PC_4), .in1(BranchAddr), .out(blezAddr), .sel(blez));
  Multiplexer #(.select(4), .width(32), .enable("false")) multiplexer_7 (
    .in0(PC_4), .in1(beqAddr), .in2(bneAddr), .in3(bgtzAddr), .in4(bltzAddr),
    .in5({PCnow[31:28], Imm, 2'b00}), .in6(RD1), .out(NPC), .sel(NPCOp));  // open: in7, in8, in9, in10, in11, in12, in13, in14, in15

  // Other names for the same wires on the sheet: j_jal[31:2] = {PCnow[31:28], Imm}; rs_jr[31:0] = RD1; zero = in_1

  // Notes on the sheet:
  //   0000:PC+4   0001:beq 0010:bne 0011:bgtz  0100:bltz  0101:jal/j  0110:jr
endmodule

module main (
  input  in_1,
  output [31:0] out_2,
  output out_3,
  output [4:0] out_4,
  output [31:0] out_5,
  output out_6,
  output [4:0] out_7,
  output [31:0] out_8
);

  wire ALUSrc, Clk, Zero;
  wire [1:0] DMOp, EXTOp, MemtoReg, RegAddr;
  wire [3:0] ALUControl, NPCOp;
  wire [31:0] ALUresult, EXTOut, MemOutData, multiplexer_3_out, NPC, PC_4, PCnow, RD1;

  NPC npc_1 (.PCnow(PCnow), .Imm(out_2[25:0]), .RD1(RD1), .PC_4(PC_4), .NPC(NPC), .NPCOp(NPCOp), .in_1(Zero));
  IFU ifu_1 (.NPC(NPC), .Instr(out_2), .in_1(Clk), .reset(in_1), .out_5(PCnow));
  Multiplexer #(.select(2), .width(5), .enable("false")) multiplexer_1 (
    .in0(out_2[20:16]), .in1(out_2[15:11]), .in2({5{1'b1}}), .out(out_4), .sel(RegAddr));  // open: in3
  Multiplexer #(.select(2), .width(32), .enable("false")) multiplexer_2 (
    .in0({ALUresult[31:7], out_7, ALUresult[1:0]}), .in1(MemOutData), .in2(PC_4), .out(out_5), .sel(MemtoReg));  // open: in3
  Controller controller_1 (
    .RW(out_3), .RegAddr(RegAddr), .ALUSrc(ALUSrc), .NPCOp(NPCOp), .MemWrite(out_6), .MemtoReg(MemtoReg),
    .EXTOp(EXTOp), .ALUControl(ALUControl), .DMOp(DMOp), .OP(out_2[31:26]), .func(out_2[5:0]));
  // Probe on EXTOp
  GRF grf_1 (
    .A1(out_2[25:21]), .A2(out_2[20:16]), .A3(out_4), .WD(out_5), .RD1(RD1), .RD2(out_8), .CLK(Clk),
    .reset(in_1), .WE(out_3));
  EXT ext_1 (.in_2(out_2[15:0]), .in_1(EXTOp), .out_3(EXTOut));
  Multiplexer #(.width(32), .enable("false")) multiplexer_3 (
    .in0(out_8), .in1(EXTOut), .out(multiplexer_3_out), .sel(ALUSrc));
  ALU alu_1 (
    .A(RD1), .B(multiplexer_3_out), .C({ALUresult[31:7], out_7, ALUresult[1:0]}), .Zero(Zero),
    .shamt(out_2[10:6]), .ALUControl(ALUControl));
  DM dm_1 (
    .ALUresult({out_7, ALUresult[1:0]}), .MemWriteData(out_8), .MemOutData(MemOutData), .in_1(Clk),
    .in_2(in_1), .in_3(out_6), .DMOp(DMOp));
  Clock clock_1 (.out(Clk));
  // Probe on out_5
  // Probe on out_8

  // Other names for the same wires on the sheet: ALUresult[6:2] = out_7; MemAdder[4:0] = out_7;
  //   funct[5:0] = out_2[5:0]; Imm16[15:0] = out_2[15:0]; Imm26[25:0] = out_2[25:0]; Instr[31:0] = out_2;
  //   shamt[4:0] = out_2[10:6]; rd[4:0] = out_2[15:11]; rt[4:0] = out_2[20:16]; rs[4:0] = out_2[25:21];
  //   OPcode[5:0] = out_2[31:26]; MemWrite = out_6; MemData[31:0] = out_8; RD2[31:0] = out_8; RegAdder[4:0] = out_4;
  //   RegData[31:0] = out_5; RegWrite = out_3; Reset = in_1
endmodule
